// Logisim project ALU.circ as structural Verilog: 9 circuits, main circuit ALU
module ALU (
  input  [31:0] Rs,
  input  [31:0] Rt,
  input  [4:0] OPcode,
  input  [3:0] Function,
  output Overflow,
  output Zero,
  output LT_Signed,
  output LT_Unsigned,
  output [31:0] ALU_Output
);

  wire alu_units_control_1_sset, or_1_out, or_2_out, or_3_out;
  wire [1:0] or_4_out;
  wire [3:0] alu_units_control_1_sll_slli, alu_units_control_1_xor_xori;
  wire [5:0] alu_units_control_1_add_addi;
  wire [31:0] Arithmetic_unit_arith_output, Logic_unit_logic_output, SET_unit_logic_output,
       Shift_unit_shift_output;

  ALU_Units_Control alu_units_control_1 (
    .Op0(OPcode[0]), .Op1(OPcode[1]), .Op2(OPcode[2]), .Op3(OPcode[3]), .Op4(OPcode[4]), .Func0(Function[0]),
    .Func1(Function[1]), .Func2(Function[2]), .Func3(Function[3]),
    .ADD_ADDI(alu_units_control_1_add_addi[0]), .SUB(alu_units_control_1_add_addi[1]),
    .SLT_SLTI(alu_units_control_1_add_addi[2]), .SLTU_SLTIU(alu_units_control_1_add_addi[3]),
    .SEQ_SEQI(alu_units_control_1_add_addi[4]), .MUL(alu_units_control_1_add_addi[5]),
    .SLL_SLLI(alu_units_control_1_sll_slli[0]), .SRL_SRLI(alu_units_control_1_sll_slli[1]),
    .SRA_SRAI(alu_units_control_1_sll_slli[2]), .ROR_RORI(alu_units_control_1_sll_slli[3]),
    .XOR_XORI(alu_units_control_1_xor_xori[0]), .OR_ORI(alu_units_control_1_xor_xori[1]),
    .AND_ANDI(alu_units_control_1_xor_xori[2]), .NOR_NORI(alu_units_control_1_xor_xori[3]),
    .SSET(alu_units_control_1_sset));  // open: SET
  Arithmetic_unit Arithmetic_unit (
    .Rs(Rs), .Rt(Rt), .Arithmetic_Control(alu_units_control_1_add_addi), .Overflow(Overflow), .Zero(Zero),
    .LT_Signed(LT_Signed), .LT_Unsigned(LT_Unsigned), .Arith_Output(Arithmetic_unit_arith_output));
  Logic_unit Logic_unit (
    .Rs(Rs), .Rt(Rt), .Logic_Control(alu_units_control_1_sll_slli), .Logic_Output(Logic_unit_logic_output));
  Shift_unit Shift_unit (
    .Rs(Rs), .Rt(Rt), .Shift_Control(alu_units_control_1_xor_xori), .Shift_Output(Shift_unit_shift_output));
  SET_unit SET_unit (
    .Rt(Rt), .SET_Control(alu_units_control_1_sset), .Logic_Output(SET_unit_logic_output));  // open: Rs
  Multiplexer #(.select(2), .width(32)) multiplexer_1 (
    .in0(Arithmetic_unit_arith_output), .in1(Logic_unit_logic_output), .in2(Shift_unit_shift_output),
    .in3(SET_unit_logic_output), .out(ALU_Output), .sel(or_4_out));  // open: en
  or or_1 (or_1_out, alu_units_control_1_add_addi[0], alu_units_control_1_add_addi[1], alu_units_control_1_add_addi[2], alu_units_control_1_add_addi[3], alu_units_control_1_add_addi[4], alu_units_control_1_add_addi[5]);
  or or_2 (or_2_out, alu_units_control_1_sll_slli[0], alu_units_control_1_sll_slli[1], alu_units_control_1_sll_slli[2], alu_units_control_1_sll_slli[3]);
  or or_3 (or_3_out, alu_units_control_1_xor_xori[0], alu_units_control_1_xor_xori[1], alu_units_control_1_xor_xori[2], alu_units_control_1_xor_xori[3]);
  or or_4 (or_4_out[0], or_1_out, alu_units_control_1_sset, or_3_out);
  or or_5 (or_4_out[1], or_3_out, alu_units_control_1_sset, or_2_out);
endmodule

module Arithmetic_unit (
  input  [31:0] Rs,
  input  [31:0] Rt,
  input  [5:0] Arithmetic_Control,
  output Overflow,
  output Zero,
  output LT_Signed,
  output LT_Unsigned,
  output [31:0] Arith_Output
);

  wire and_1_out, and_2_out, and_3_out, and_4_out, and_5_out, and_6_out, comparator_1_eq, comparator_1_lt,
       comparator_2_eq, comparator_5_gt, comparator_5_lt, comparator_6_gt, comparator_6_lt, comparator_7_gt,
       comparator_7_lt, comparator_8_gt, comparator_8_lt, comparator_9_gt, comparator_9_lt, or_4_out,
       or_5_out;
  wire [2:0] or_3_out;
  wire [31:0] ADD___ADDI, MUL, SEQ___SEQI, SLT___SLTI, SLTU___SLTIU, SUB;

  Adder #(.width(32)) adder_1 (.a(Rs), .b(Rt), .out(ADD___ADDI));  // open: cin, cout
  Subtractor #(.width(32)) subtractor_1 (.a(Rs), .b(Rt), .out(SUB));  // open: bin, bout
  Multiplier #(.width(32)) multiplier_1 (.a(Rs), .b(Rt), .out(MUL));  // open: cin, cout
  Comparator #(.width(32)) comparator_1 (.a(Rs), .b(Rt), .eq(comparator_1_eq), .lt(comparator_1_lt));  // open: gt
  Comparator #(.width(32), .mode("unsigned")) comparator_2 (.a(Rs), .b(Rt), .eq(comparator_2_eq));  // open: gt, lt
  Comparator #(.width(32)) comparator_3 (.a(Rs), .b(Rt), .eq(Zero), .lt(LT_Signed));  // open: gt
  Comparator #(.width(32), .mode("unsigned")) comparator_4 (.a(Rs), .b(Rt), .lt(LT_Unsigned));  // open: gt, eq
  assign SEQ___SEQI = {{31{1'b0}}, comparator_1_eq};  // Bit_Extender bit_extender_1
  assign SLT___SLTI = {{31{1'b0}}, comparator_1_lt};  // Bit_Extender bit_extender_2
  assign SLTU___SLTIU = {{31{1'b0}}, comparator_2_eq};  // Bit_Extender bit_extender_3
  // Probe on Arith_Output
  Multiplexer #(.select(3), .width(32)) multiplexer_1 (
    .in0(ADD___ADDI), .in1(SUB), .in2(SLT___SLTI), .in3(SLTU___SLTIU), .in4(SEQ___SEQI), .in5(MUL),
    .out(Arith_Output), .sel(or_3_out));  // open: in6, in7, en
  or or_1 (or_3_out[2], Arithmetic_Control[4], Arithmetic_Control[5]);
  or or_2 (or_3_out[1], Arithmetic_Control[2], Arithmetic_Control[3]);
  or or_3 (or_3_out[0], Arithmetic_Control[1], Arithmetic_Control[3], Arithmetic_Control[5]);
  Comparator #(.width(32)) comparator_5 (
    .a(Rs), .b({32{1'b0}}), .gt(comparator_5_gt), .lt(comparator_5_lt));  // open: eq
  Comparator #(.width(32)) comparator_6 (
    .a(Rt), .b({32{1'b0}}), .gt(comparator_6_gt), .lt(comparator_6_lt));  // open: eq
  Comparator #(.width(32)) comparator_7 (
    .a(ADD___ADDI), .b({32{1'b0}}), .gt(comparator_7_gt), .lt(comparator_7_lt));  // open: eq
  Comparator #(.width(32)) comparator_8 (
    .a(SUB), .b({32{1'b0}}), .gt(comparator_8_gt), .lt(comparator_8_lt));  // open: eq
  Comparator #(.width(32)) comparator_9 (.a(Rs), .b(Rt), .gt(comparator_9_gt), .lt(comparator_9_lt));  // open: eq
  and and_1 (and_1_out, comparator_5_gt, comparator_6_gt, comparator_7_lt);
  and and_2 (and_2_out, comparator_7_gt, comparator_6_lt, comparator_5_lt);
  and and_3 (and_3_out, comparator_8_lt, comparator_9_gt);
  and and_4 (and_4_out, comparator_8_gt, comparator_9_lt);
  or or_4 (or_4_out, and_1_out, and_2_out);
  or or_5 (or_5_out, and_3_out, and_4_out);
  and and_5 (and_5_out, or_4_out, Arithmetic_Control[0]);
  or or_6 (Overflow, and_5_out, and_6_out);
  and and_6 (and_6_out, or_5_out, Arithmetic_Control[1]);

  // Notes on the sheet:
  //   JALR, LW, SW func. will use ADD
endmodule

module Logic_unit (
  input  [31:0] Rs,
  input  [31:0] Rt,
  input  [3:0] Logic_Control,
  output [31:0] Logic_Output
);

  wire [1:0] or_2_out;
  wire [31:0] AND___ANDI, NOR___NORI, OR___ORI, XOR___XORI;

  assign AND___ANDI = Rs & Rt;  // AND_Gate AND, 32 bits wide
  assign OR___ORI = Rs | Rt;  // OR_Gate OR, 32 bits wide
  assign NOR___NORI = ~(Rs | Rt);  // NOR_Gate NOR, 32 bits wide
  assign XOR___XORI = Rs ^ Rt;  // XOR_Gate XOR, 32 bits wide
  Multiplexer #(.select(2), .width(32)) multiplexer_1 (
    .in0(XOR___XORI), .in1(OR___ORI), .in2(AND___ANDI), .in3(NOR___NORI), .out(Logic_Output), .sel(or_2_out));  // open: en
  or or_2 (or_2_out[0], Logic_Control[1], Logic_Control[3]);
  or or_3 (or_2_out[1], Logic_Control[2], Logic_Control[3]);
endmodule

module Shift_unit (
  input  [31:0] Rs,
  input  [31:0] Rt,
  input  [3:0] Shift_Control,
  output [31:0] Shift_Output
);

  wire [1:0] or_1_out;
  wire [31:0] ROR____RORI, ROR___RORI, SLL___SLLI, SRA___SRAI, SRL___SRLI;

  Shifter #(.width(32)) shifter_1 (.in(Rs), .\dist (Rt[4:0]), .out(SLL___SLLI));
  Shifter #(.width(32), .shift("lr")) shifter_2 (.in(Rs), .\dist (Rt[4:0]), .out(SRL___SRLI));
  Shifter #(.width(32), .shift("ar")) shifter_3 (.in(Rs), .\dist (Rt[4:0]), .out(SRA___SRAI));
  Shifter #(.width(32), .shift("rr")) shifter_4 (.in(Rs), .\dist (Rt[4:0]), .out(ROR___RORI));
  Multiplexer #(.select(2), .width(32)) multiplexer_1 (
    .in0(SLL___SLLI), .in1(SRL___SRLI), .in2(SRA___SRAI), .in3(ROR____RORI), .out(Shift_Output),
    .sel(or_1_out));  // open: en
  or or_1 (or_1_out[0], Shift_Control[1], Shift_Control[3]);
  or or_2 (or_1_out[1], Shift_Control[2], Shift_Control[3]);

  // Notes on the sheet:
  //   SLL
endmodule

module control (
  input  f4,
  input  f3,
  input  f2,
  input  f1,
  input  op4,
  input  op3,
  input  op2,
  input  op1,
  output AddAddI,
  output Sub,
  output SltSltI,
  output SltuSltIu,
  output SeqSeqI,
  output Mul,
  output SllSllI,
  output SrlSrlI,
  output SraSraI,
  output RorRorI,
  output XorXorI,
  output OrOrI,
  output AndAndI,
  output NorNorI
);

  wire and_1_out, and_2_out, and_4_out, and_5_out, and_6_out, and_7_out, and_8_out, and_9_out, and_11_out,
       and_12_out, and_13_out, and_14_out, and_15_out, and_16_out, and_17_out, and_18_out, and_19_out,
       and_20_out, and_21_out, and_22_out, and_23_out, and_24_out, and_25_out, and_26_out, nand_1_out,
       nand_2_out, nand_3_out, nand_4_out, nand_5_out, nand_6_out, nand_7_out, nand_8_out, nand_9_out,
       nand_10_out, nand_11_out, nand_12_out, nand_13_out, not_1_out, not_2_out, not_3_out, not_4_out,
       not_5_out, not_6_out, not_7_out, not_8_out, not_9_out, not_10_out, not_11_out, not_12_out, not_13_out,
       not_14_out, not_15_out, not_16_out, not_17_out, not_18_out, not_19_out, not_20_out, not_21_out,
       not_22_out, not_23_out, not_24_out, not_25_out, not_26_out, not_27_out, not_28_out, not_29_out,
       not_30_out, not_31_out, not_32_out, not_33_out, not_34_out;

  nand nand_1 (nand_1_out, op1, op2, op3, op4, f4, f2, f1);
  not not_1 (not_1_out, op4);
  not not_2 (not_2_out, op2);
  nand nand_2 (nand_2_out, op1, op2, op3, op4, f4, f2);
  nand nand_3 (nand_3_out, op1, op2, op3, op4, f4, f1);
  not not_3 (not_3_out, op4);
  not not_4 (not_4_out, op1);
  nand nand_4 (nand_4_out, op1, op2, op3, op4, f4);
  not not_5 (not_5_out, op4);
  nand nand_5 (nand_5_out, op1, op2, op3, op4, f3, f2, f1);
  not not_6 (not_6_out, op3);
  not not_7 (not_7_out, op2);
  not not_8 (not_8_out, op1);
  nand nand_6 (nand_6_out, op1, op2, op3, op4, f2);
  not not_9 (not_9_out, op1);
  not not_10 (not_10_out, op2);
  not not_11 (not_11_out, op3);
  not not_12 (not_12_out, op4);
  not not_13 (not_13_out, f4);
  not not_14 (not_14_out, f3);
  not not_15 (not_15_out, f2);
  not not_16 (not_16_out, f1);
  not not_17 (not_17_out, op4);
  not not_18 (not_18_out, op3);
  not not_19 (not_19_out, op2);
  nand nand_7 (nand_7_out, op1, op2, op3, op4, f4, f3, f2);
  not not_20 (not_20_out, op4);
  not not_21 (not_21_out, op3);
  not not_22 (not_22_out, op1);
  nand nand_8 (nand_8_out, op1, op2, op3, op4, f4, f3, f1);
  not not_23 (not_23_out, op4);
  not not_24 (not_24_out, op3);
  nand nand_9 (nand_9_out, op1, op2, op3, op4, f4, f3);
  not not_25 (not_25_out, op4);
  not not_26 (not_26_out, op2);
  not not_27 (not_27_out, op1);
  nand nand_10 (nand_10_out, op1, op2, op3, op4, f3, f2);
  not not_28 (not_28_out, op3);
  not not_29 (not_29_out, op2);
  nand nand_11 (nand_11_out, op1, op2, op3, op4, f3, f1);
  not not_30 (not_30_out, op3);
  not not_31 (not_31_out, op1);
  nand nand_12 (nand_12_out, op1, op2, op3, op4, f3);
  not not_32 (not_32_out, op3);
  nand nand_13 (nand_13_out, op1, op2, op3, op4, f2, f1);
  not not_33 (not_33_out, op2);
  not not_34 (not_34_out, op1);
  and and_1 (and_1_out, nand_1_out, f3);
  and and_2 (and_2_out, not_1_out, op3, not_2_out, op1);
  and and_3 (Sub, nand_2_out, f3, f1);
  and and_4 (and_4_out, nand_3_out, f3, f2);
  and and_5 (and_5_out, not_3_out, op3, op2, not_4_out);
  and and_6 (and_6_out, nand_4_out, f3, f2, f1);
  and and_7 (and_7_out, not_5_out, op3, op2, op1);
  and and_8 (and_8_out, nand_5_out, f4);
  and and_9 (and_9_out, op4, not_6_out, not_7_out, not_8_out);
  and and_10 (Mul, nand_6_out, f4, f3, f1);
  and and_11 (and_11_out, not_9_out, not_10_out, not_11_out, not_12_out, not_13_out, not_14_out, not_15_out, not_16_out);
  or or_1 (SllSllI, and_11_out, and_12_out);
  and and_12 (and_12_out, not_17_out, not_18_out, not_19_out, op1);
  and and_13 (and_13_out, nand_7_out, f1);
  and and_14 (and_14_out, not_20_out, not_21_out, op2, not_22_out);
  and and_15 (and_15_out, nand_8_out, f2);
  and and_16 (and_16_out, not_23_out, not_24_out, op2, op1);
  and and_17 (and_17_out, nand_9_out, f2, f1);
  and and_18 (and_18_out, not_25_out, op3, not_26_out, not_27_out);
  and and_19 (and_19_out, nand_10_out, f4, f1);
  and and_20 (and_20_out, op4, not_28_out, not_29_out, op1);
  and and_21 (and_21_out, nand_11_out, f4, f2);
  and and_22 (and_22_out, op4, not_30_out, op2, not_31_out);
  and and_23 (and_23_out, nand_12_out, f4, f2, f1);
  and and_24 (and_24_out, op4, not_32_out, op2, op1);
  and and_25 (and_25_out, nand_13_out, f4, f3);
  and and_26 (and_26_out, op4, op3, not_33_out, not_34_out);
  buf or_2 (AddAddI, and_2_out);  // OR_Gate
  or or_3 (SltSltI, and_4_out, and_5_out);
  or or_4 (SltuSltIu, and_6_out, and_7_out);
  or or_5 (SeqSeqI, and_8_out, and_9_out);
  or or_6 (SrlSrlI, and_13_out, and_14_out);
  or or_7 (SraSraI, and_15_out, and_16_out);
  or or_8 (RorRorI, and_17_out, and_18_out);
  or or_9 (XorXorI, and_19_out, and_20_out);
  or or_10 (OrOrI, and_21_out, and_22_out);
  or or_11 (AndAndI, and_23_out, and_24_out);
  or or_12 (NorNorI, and_25_out, and_26_out);
endmodule

module ALU_Units_Control (
  input  Op0,
  input  Op1,
  input  Op2,
  input  Op3,
  input  Op4,
  input  Func0,
  input  Func1,
  input  Func2,
  input  Func3,
  output ADD_ADDI,
  output SUB,
  output SLT_SLTI,
  output SLTU_SLTIU,
  output SEQ_SEQI,
  output MUL,
  output SLL_SLLI,
  output SRL_SRLI,
  output SRA_SRAI,
  output ROR_RORI,
  output XOR_XORI,
  output OR_ORI,
  output AND_ANDI,
  output NOR_NORI,
  output SET,
  output SSET
);

  wire and_3_out, and_4_out, and_5_out, and_6_out, and_8_out, and_9_out, and_10_out, and_11_out, and_12_out,
       and_13_out, and_15_out, and_16_out, and_17_out, and_18_out, and_19_out, and_20_out, and_21_out,
       and_22_out, and_23_out, and_24_out, and_25_out, and_26_out, and_27_out, and_28_out, and_29_out,
       nor_1_out, nor_2_out, nor_3_out, nor_4_out, nor_5_out, nor_6_out, nor_7_out, nor_8_out, nor_9_out,
       nor_10_out, nor_11_out, nor_12_out, nor_13_out, nor_14_out, nor_15_out, nor_16_out, nor_17_out,
       nor_18_out, nor_19_out, nor_20_out, nor_21_out, nor_22_out, nor_23_out, nor_24_out, nor_25_out,
       nor_26_out, nor_27_out, nor_28_out, nor_29_out, not_1_out;

  nor nor_1 (nor_1_out, Op1, Op4);
  nor nor_2 (nor_2_out, Op0, Op4);
  nor nor_3 (nor_3_out, Op0, Op1, Op2, Op3, Op4, Func0, Func1, Func3);
  nor nor_4 (nor_4_out, Op1, Op3, Op4);
  not not_1 (not_1_out, Op4);
  nor nor_5 (nor_5_out, Op1, Op2, Op3);
  nor nor_6 (nor_6_out, Op0, Op1, Op2, Op3, Op4, Func1, Func3);
  nor nor_7 (nor_7_out, Op0, Op1, Op2, Op3, Op4, Func0, Func3);
  nor nor_8 (nor_8_out, Op0, Op3, Op4);
  nor nor_9 (nor_9_out, Op0, Op1, Op2, Op3, Op4, Func3);
  nor nor_10 (nor_10_out, Op3, Op4);
  nor nor_11 (nor_11_out, Op0, Op1, Op2, Op3, Op4, Func0, Func1, Func2);
  nor nor_12 (nor_12_out, Op0, Op1, Op2, Op4);
  nor nor_13 (nor_13_out, Op0, Op1, Op2, Op3, Op4, Func1);
  nor nor_14 (nor_14_out, Op1, Op2, Op3, Op4);
  nor nor_15 (nor_15_out, Op0, Op1, Op2, Op3, Op4, Func1, Func2, Func3);
  nor nor_16 (nor_16_out, Op0, Op2, Op3, Op4);
  nor nor_17 (nor_17_out, Op0, Op1, Op2, Op3, Op4, Func0, Func2, Func3);
  nor nor_18 (nor_18_out, Op2, Op3, Op4);
  nor nor_19 (nor_19_out, Op0, Op1, Op2, Op3, Op4, Func2, Func3);
  nor nor_20 (nor_20_out, Op0, Op1, Op3, Op4);
  nor nor_21 (nor_21_out, Op0, Op1, Op2, Op3, Op4, Func1, Func2);
  nor nor_22 (nor_22_out, Op1, Op2, Op4);
  nor nor_23 (nor_23_out, Op0, Op1, Op2, Op3, Op4, Func0, Func2);
  nor nor_24 (nor_24_out, Op0, Op2, Op4);
  nor nor_25 (nor_25_out, Op0, Op1, Op2, Op3, Op4, Func2);
  nor nor_26 (nor_26_out, Op2, Op4);
  nor nor_27 (nor_27_out, Op0, Op1, Op2, Op3, Op4, Func0, Func1);
  nor nor_28 (nor_28_out, Op0, Op1, Op4);
  and and_1 (SET, nor_1_out, Op0, Op2, Op3);
  and and_2 (SSET, nor_2_out, Op1, Op2, Op3);
  and and_3 (and_3_out, nor_3_out, Func2);
  and and_4 (and_4_out, nor_4_out, Op0, Op2);
  and and_5 (and_5_out, not_1_out, Op0, Op1, Op2, Op3);
  and and_6 (and_6_out, nor_5_out, Op0, Op4);
  and and_7 (SUB, nor_6_out, Func0, Func2);
  and and_8 (and_8_out, nor_7_out, Func1, Func2);
  and and_9 (and_9_out, nor_8_out, Op1, Op2);
  and and_10 (and_10_out, nor_9_out, Func0, Func1, Func2);
  and and_11 (and_11_out, nor_10_out, Op0, Op1, Op2);
  and and_12 (and_12_out, nor_11_out, Func3);
  and and_13 (and_13_out, nor_12_out, Op3);
  and and_14 (MUL, nor_13_out, Func0, Func2, Func3);
  nor nor_29 (nor_29_out, Op0, Op1, Op2, Op3, Func0, Func1, Func2, Func3);
  and and_15 (and_15_out, nor_14_out, Op0);
  and and_16 (and_16_out, nor_15_out, Func0);
  and and_17 (and_17_out, nor_16_out, Op1);
  and and_18 (and_18_out, nor_17_out, Func1);
  and and_19 (and_19_out, nor_18_out, Op0, Op1);
  and and_20 (and_20_out, nor_19_out, Func0, Func1);
  and and_21 (and_21_out, nor_20_out, Op2);
  and and_22 (and_22_out, nor_21_out, Func0, Func3);
  and and_23 (and_23_out, nor_22_out, Op0, Op3);
  and and_24 (and_24_out, nor_23_out, Func1, Func3);
  and and_25 (and_25_out, nor_24_out, Op1, Op3);
  and and_26 (and_26_out, nor_25_out, Func0, Func1, Func3);
  and and_27 (and_27_out, nor_26_out, Op0, Op1, Op3);
  and and_28 (and_28_out, nor_27_out, Func2, Func3);
  and and_29 (and_29_out, nor_28_out, Op2, Op3);
  or or_1 (ADD_ADDI, and_3_out, and_4_out, and_5_out, and_6_out);
  or or_2 (SLT_SLTI, and_8_out, and_9_out);
  or or_3 (SLTU_SLTIU, and_10_out, and_11_out);
  or or_4 (SEQ_SEQI, and_12_out, and_13_out);
  or or_5 (SLL_SLLI, nor_29_out, and_15_out);
  or or_6 (SRL_SRLI, and_16_out, and_17_out);
  or or_7 (SRA_SRAI, and_18_out, and_19_out);
  or or_8 (ROR_RORI, and_20_out, and_21_out);
  or or_9 (XOR_XORI, and_22_out, and_23_out);
  or or_10 (OR_ORI, and_24_out, and_25_out);
  or or_11 (AND_ANDI, and_26_out, and_27_out);
  or or_12 (NOR_NORI, and_28_out, and_29_out);
endmodule

module NEW_Arithmetic_Control (
  input  Op0,
  input  Op1,
  input  Op2,
  input  Op3,
  input  Op4,
  input  Func0,
  input  Func1,
  input  Func2,
  input  Func3,
  output ADD_ADDI,
  output SUB,
  output SLT_SLTI,
  output SLTU_SLTIU,
  output SEQ_SEQI,
  output MUL
);

  wire and_1_out, and_2_out, and_3_out, and_4_out, and_6_out, and_7_out, and_8_out, and_9_out, and_10_out,
       and_11_out, nor_1_out, nor_2_out, nor_3_out, nor_4_out, nor_5_out, nor_6_out, nor_7_out, nor_8_out,
       nor_9_out, nor_10_out, nor_11_out, not_1_out;

  nor nor_1 (nor_1_out, Op0, Op1, Op2, Op3, Op4, Func0, Func1, Func3);
  nor nor_2 (nor_2_out, Op1, Op3, Op4);
  not not_1 (not_1_out, Op4);
  nor nor_3 (nor_3_out, Op1, Op2, Op3);
  nor nor_4 (nor_4_out, Op0, Op1, Op2, Op3, Op4, Func1, Func3);
  nor nor_5 (nor_5_out, Op0, Op1, Op2, Op3, Op4, Func0, Func3);
  nor nor_6 (nor_6_out, Op0, Op3, Op4);
  nor nor_7 (nor_7_out, Op0, Op1, Op2, Op3, Op4, Func3);
  nor nor_8 (nor_8_out, Op3, Op4);
  nor nor_9 (nor_9_out, Op0, Op1, Op2, Op3, Op4, Func0, Func1, Func2);
  nor nor_10 (nor_10_out, Op0, Op1, Op2, Op4);
  nor nor_11 (nor_11_out, Op0, Op1, Op2, Op3, Op4, Func1);
  and and_1 (and_1_out, nor_1_out, Func2);
  and and_2 (and_2_out, nor_2_out, Op0, Op2);
  and and_3 (and_3_out, not_1_out, Op0, Op1, Op2, Op3);
  and and_4 (and_4_out, nor_3_out, Op0, Op4);
  and and_5 (SUB, nor_4_out, Func0, Func2);
  and and_6 (and_6_out, nor_5_out, Func1, Func2);
  and and_7 (and_7_out, nor_6_out, Op1, Op2);
  and and_8 (and_8_out, nor_7_out, Func0, Func1, Func2);
  and and_9 (and_9_out, nor_8_out, Op0, Op1, Op2);
  and and_10 (and_10_out, nor_9_out, Func3);
  and and_11 (and_11_out, nor_10_out, Op3);
  and and_12 (MUL, nor_11_out, Func0, Func2, Func3);
  or or_1 (ADD_ADDI, and_1_out, and_2_out, and_3_out, and_4_out);
  or or_2 (SLT_SLTI, and_6_out, and_7_out);
  or or_3 (SLTU_SLTIU, and_8_out, and_9_out);
  or or_4 (SEQ_SEQI, and_10_out, and_11_out);
endmodule

module NEW_Shift_Logic_Control (
  input  Op0,
  input  Op1,
  input  Op2,
  input  Op3,
  input  Op4,
  input  Func1,
  input  Func2,
  input  Func3,
  input  Func4,
  output SLL_SLLI,
  output SRL_SRLI,
  output SRA_SRAI,
  output ROR_RORI,
  output XOR_XORI,
  output OR_ORI,
  output AND_ANDI,
  output NOR_NORI
);

  wire and_1_out, and_2_out, and_3_out, and_4_out, and_5_out, and_6_out, and_7_out, and_8_out, and_9_out,
       and_10_out, and_11_out, and_12_out, and_13_out, and_14_out, and_15_out, nor_1_out, nor_2_out,
       nor_3_out, nor_4_out, nor_5_out, nor_6_out, nor_7_out, nor_8_out, nor_9_out, nor_10_out, nor_11_out,
       nor_12_out, nor_13_out, nor_14_out, nor_15_out, nor_16_out;

  nor nor_1 (nor_1_out, Op1, Op2, Op3, Op4);
  nor nor_2 (nor_2_out, Op0, Op1, Op2, Op3, Op4, Func2, Func3, Func4);
  nor nor_3 (nor_3_out, Op0, Op2, Op3, Op4);
  nor nor_4 (nor_4_out, Op0, Op1, Op2, Op3, Op4, Func1, Func3, Func4);
  nor nor_5 (nor_5_out, Op2, Op3, Op4);
  nor nor_6 (nor_6_out, Op0, Op1, Op2, Op3, Op4, Func3, Func4);
  nor nor_7 (nor_7_out, Op0, Op1, Op3, Op4);
  nor nor_8 (nor_8_out, Op0, Op1, Op2, Op3, Op4, Func2, Func3);
  nor nor_9 (nor_9_out, Op1, Op2, Op4);
  nor nor_10 (nor_10_out, Op0, Op1, Op2, Op3, Op4, Func1, Func3);
  nor nor_11 (nor_11_out, Op0, Op2, Op4);
  nor nor_12 (nor_12_out, Op0, Op1, Op2, Op3, Op4, Func3);
  nor nor_13 (nor_13_out, Op2, Op4);
  nor nor_14 (nor_14_out, Op0, Op1, Op2, Op3, Op4, Func1, Func2);
  nor nor_15 (nor_15_out, Op0, Op1, Op4);
  nor nor_16 (nor_16_out, Op0, Op1, Op2, Op3, Func1, Func2, Func3, Func4);
  and and_1 (and_1_out, nor_1_out, Op0);
  and and_2 (and_2_out, nor_2_out, Func1);
  and and_3 (and_3_out, nor_3_out, Op1);
  and and_4 (and_4_out, nor_4_out, Func2);
  and and_5 (and_5_out, nor_5_out, Op0, Op1);
  and and_6 (and_6_out, nor_6_out, Func1, Func2);
  and and_7 (and_7_out, nor_7_out, Op2);
  and and_8 (and_8_out, nor_8_out, Func1, Func4);
  and and_9 (and_9_out, nor_9_out, Op0, Op3);
  and and_10 (and_10_out, nor_10_out, Func2, Func4);
  and and_11 (and_11_out, nor_11_out, Op1, Op3);
  and and_12 (and_12_out, nor_12_out, Func1, Func2, Func4);
  and and_13 (and_13_out, nor_13_out, Op0, Op1, Op3);
  and and_14 (and_14_out, nor_14_out, Func3, Func4);
  and and_15 (and_15_out, nor_15_out, Op2, Op3);
  or or_1 (SLL_SLLI, nor_16_out, and_1_out);
  or or_2 (SRL_SRLI, and_2_out, and_3_out);
  or or_3 (SRA_SRAI, and_4_out, and_5_out);
  or or_4 (ROR_RORI, and_6_out, and_7_out);
  or or_5 (XOR_XORI, and_8_out, and_9_out);
  or or_6 (OR_ORI, and_10_out, and_11_out);
  or or_7 (AND_ANDI, and_12_out, and_13_out);
  or or_8 (NOR_NORI, and_14_out, and_15_out);
endmodule

module SET_unit (
  input  [31:0] Rs,
  input  [31:0] Rt,
  input  SET_Control,
  output [31:0] Logic_Output
);

  wire undriven;
  wire [31:0] shifter_1_out, shifter_2_out, SSET;

  Shifter #(.width(32)) shifter_1 (.in(Rs), .\dist (5'b01111), .out(shifter_1_out));
  Shifter #(.width(32)) shifter_2 (.in(shifter_1_out), .\dist (5'b00001), .out(shifter_2_out));
  assign SSET = shifter_2_out | Rt;  // OR_Gate or_1, 32 bits wide
  Multiplexer #(.width(32)) multiplexer_1 (.in0(Rt), .in1(SSET), .out(Logic_Output), .sel(undriven));  // open: en

  // Other names for the same wires on the sheet: SET[31:0] = Rt
endmodule
