// Logisim project Control_Unit.circ as structural Verilog: 5 circuits, main circuit Control Signal Unit
module Control_Signal_Unit (
  input  in_1,
  input  [5:0] OP6,
  output Jump,
  output Kill1,
  output out_5,
  output Kill2,
  output out_7,
  output out_8,
  output out_9,
  output [1:0] out_10,
  output out_11,
  output out_12,
  output out_13
);

  wire j_branch_1_jump;

  J_Branch j_branch_1 (._6_bit_Op(OP6), .Jump(j_branch_1_jump));
  AluSrc_Ex_Control alusrc_ex_control_1 (.Ext_Op(out_11), .in_1(OP6), .Alu_Src(out_12));
  Imm_Select imm_select_1 (.Imm_Select(out_13), .in_1(OP6));
  Storage_Control_Unit storage_control_unit_1 (
    .RegSrc(out_5), .RegWr(out_7), .MemRd(out_8), .MemWr(out_9), .MemtoReg(out_10), .in_1(OP6));
  PC_Pipeline pc_pipeline_1 (.J(j_branch_1_jump), .B(in_1), .Jump(Jump), .Kill1(Kill1), .Kill2(Kill2));  // open: Bransh
endmodule

module Imm_Select (
  input  [5:0] in_1,
  output Imm_Select
);

  wire and_1_out, and_2_out, and_3_out;

  and and_1 (and_1_out, in_1[4], in_1[0]);
  and and_2 (and_2_out, in_1[4], in_1[1]);
  and and_3 (and_3_out, in_1[4], in_1[2]);
  or or_1 (Imm_Select, and_1_out, and_2_out, and_3_out);

  // Other names for the same wires on the sheet: Op0 = in_1[0]; Op1 = in_1[1]; Op2 = in_1[2]; Op3 = in_1[3];
  //   Op4 = in_1[4]; Op5 = in_1[5]
endmodule

module AluSrc_Ex_Control (
  input  [5:0] in_1,
  output Ext_Op,
  output Alu_Src
);

  wire and_1_out, and_2_out, and_3_out, and_4_out, and_5_out, and_6_out, and_7_out, and_8_out, not_1_out,
       not_2_out, not_3_out, not_4_out, not_5_out, not_6_out, not_7_out, not_8_out, not_9_out, not_10_out,
       not_11_out;

  not not_1 (not_1_out, in_1[3]);
  not not_2 (not_2_out, in_1[0]);
  not not_3 (not_3_out, in_1[2]);
  not not_4 (not_4_out, in_1[1]);
  not not_5 (not_5_out, in_1[0]);
  not not_6 (not_6_out, in_1[1]);
  not not_7 (not_7_out, in_1[4]);
  not not_8 (not_8_out, in_1[4]);
  not not_9 (not_9_out, in_1[4]);
  not not_10 (not_10_out, in_1[2]);
  not not_11 (not_11_out, in_1[1]);
  and and_1 (and_1_out, not_1_out, not_2_out);
  and and_2 (and_2_out, not_3_out, not_4_out, not_5_out);
  and and_3 (and_3_out, in_1[2], not_6_out, in_1[0]);
  and and_4 (and_4_out, in_1[3], in_1[2], in_1[1]);
  and and_5 (and_5_out, not_7_out, in_1[0]);
  and and_6 (and_6_out, not_8_out, in_1[1]);
  and and_7 (and_7_out, not_9_out, in_1[2]);
  and and_8 (and_8_out, in_1[4], not_10_out, not_11_out);
  or or_1 (Ext_Op, and_1_out, and_2_out, and_3_out, and_4_out, in_1[4]);
  or or_2 (Alu_Src, and_5_out, and_6_out, and_7_out, in_1[3], and_8_out);

  // Other names for the same wires on the sheet: Op0 = in_1[0]; Op1 = in_1[1]; Op2 = in_1[2]; Op3 = in_1[3];
  //   Op4 = in_1[4]
endmodule

module J_Branch (
  input  [5:0] _6_bit_Op,
  output Jump
);

  wire not_1_out;

  not not_1 (not_1_out, _6_bit_Op[4]);
  and and_1 (Jump, not_1_out, _6_bit_Op[3], _6_bit_Op[2], _6_bit_Op[1], _6_bit_Op[0]);

  // Other names for the same wires on the sheet: Op0 = _6_bit_Op[0]; Op1 = _6_bit_Op[1]; Op2 = _6_bit_Op[2];
  //   Op3 = _6_bit_Op[3]; Op4 = _6_bit_Op[4]
endmodule

module PC_Pipeline (
  input  J,
  input  B,
  output Jump,
  output Bransh,
  output Kill1,
  output Kill2
);

  wire not_1_out;

  not not_1 (not_1_out, B);
  and and_1 (Jump, J, not_1_out);
  or or_1 (Kill1, Jump, B);

  assign Bransh = B;
  assign Kill2 = B;
endmodule
