// Logisim project Control_Unit_Final.circ as structural Verilog: 2 circuits, main circuit Control Signal Unit
module Control_Signal_Unit (
  input  [5:0] OP6,
  output out_2,
  output out_3,
  output out_4,
  output out_5,
  output out_6,
  output out_7,
  output out_8,
  output out_9,
  output out_10
);

  J_Branch j_branch_1 (._6_bit_Op(OP6), .Jump(out_2));  // open: Branch
  Op_Control op_control_1 (.ExtOp(out_8), .ALUSrc(out_9), ._6_bit_Op(OP6));
  Imm_Select imm_select_1 (.Imm_Select(out_10), .in_1(OP6));
  Storage_Control_Unit storage_control_unit_1 (
    .RegSrc(out_3), .RegWr(out_4), .MemRd(out_5), .MemWr(out_6), .MemtoReg(out_7), .in_1(OP6));
endmodule

module Imm_Select (
  input  [5:0] in_1,
  output Imm_Select
);

  wire and_1_out, and_2_out, and_3_out;

  and and_1 (and_1_out, in_1[4], in_1[0]);
  and and_2 (and_2_out, in_1[4], in_1[1]);
  and and_3 (and_3_out, in_1[4], in_1[2]);
  or or_1 (Imm_Select, and_1_out, and_2_out, and_3_out);

  // Other names for the same wires on the sheet: Op0 = in_1[0]; Op1 = in_1[1]; Op2 = in_1[2]; Op3 = in_1[3];
  //   Op4 = in_1[4]; Op5 = in_1[5]
endmodule
