// Logisim project Data_Memory.circ as structural Verilog: 1 circuit, main circuit Data_Memory
// Data Memory
module Data_Memory (
  input  [31:0] Address,
  input  [31:0] Data_In,
  input  Memory_Write,
  input  Memory_Read,
  input  Clock,
  output [31:0] Data_Out
);

  RAM #(.addrWidth(20), .dataWidth(32), .bus("separate")) ram_1 (
    .addr(Address[19:0]), .din(Data_In), .data(Data_Out), .str(Memory_Write), .sel(1'b1), .clk(Clock),
    .ld(Memory_Read));  // open: clr
endmodule
