// Logisim project Instruction_Memory.circ as structural Verilog: 1 circuit, main circuit Instruction Memory
module Instruction_Memory (
  input  [19:0] PC,
  output [31:0] _32_bit_iinstruction
);

  ROM #(.addrWidth(20), .dataWidth(32)) rom_1 (.addr(PC), .data(_32_bit_iinstruction));  // open: sel

  // Notes on the sheet:
  //   INSTRUCTION MEMORY
  //   contents of rom_1 (hex, n*v repeats v):
  //   1004d 10011 10051 a008d 20091 128900cd 45ac00ce 230711 500010d 7342010e 240751 384004d 1234020d
  //   5678020e 140945 12508c0 834100 50 10090 200d0 a42100 841100 c31180 30d2 820880 ffe00712 40011
  //   1a31280 245380 4453c0 57684 2501cf 4545024d 4545028d 95095 ffff0dcb 12 1431140 50 50890 608d0
  //   1631100 40011 380f
endmodule
