// Logisim project Instruction_Memory_1.circ as structural Verilog: 1 circuit, main circuit main
module main (
  input  [19:0] Pc,
  input  Clk
);

  wire [4:0] ram_1_data_2, ram_1_data_3, ram_1_data_4;
  wire [5:0] ram_1_data;
  wire [10:0] ram_1_data_5;

  RAM #(.addrWidth(20), .dataWidth(32)) ram_1 (
    .addr(Pc), .we(1'b0), .oe(1'b1), .clk(Clk),
    .data({ram_1_data_5, ram_1_data_4, ram_1_data_3, ram_1_data_2, ram_1_data}));

  // Notes on the sheet:
  //   INSTRUCTION MEMORY
  //   R_Tube
  //   I-Type
  //   SB_Type
endmodule
