// Logisim project Instruction_Memory_2.circ as structural Verilog: 1 circuit, main circuit main
module main (
  input  [19:0] Pc,
  input  Clk,
  input  [19:0] in_3,
  input  Clk_2
);

  wire ram_1_p3;
  wire [4:0] ram_2_data_2, ram_2_data_3, ram_2_data_4;
  wire [5:0] ram_2_data;
  wire [10:0] ram_2_data_5;

  // RAM #(.addrWidth(20), .dataWidth(32)) ram_1: pin names not known; wires that end beside it: Pc, 1'b0, ram_1_p3, Clk
  RAM #(.addrWidth(20), .dataWidth(32), .bus("separate")) ram_2 (
    .addr(in_3), .data({ram_2_data_5, ram_2_data_4, ram_2_data_3, ram_2_data_2, ram_2_data}), .str(1'b0),
    .clk(Clk_2), .ld(1'b1));  // open: din, sel, clr

  // Notes on the sheet:
  //   INSTRUCTION MEMORY
  //   R_Tube
  //   I-Type
  //   SB_Type
endmodule
