// Logisim project J_Branch_control.circ as structural Verilog
module J_Branch_control (
  input  [5:0] _6_bit_Op,
  output Branch,
  output Jump
);

  wire and_1_out, and_2_out, not_1_out, not_2_out, not_3_out;

  not not_1 (not_1_out, _6_bit_Op[3]);
  not not_2 (not_2_out, _6_bit_Op[3]);
  not not_3 (not_3_out, _6_bit_Op[4]);
  and and_1 (and_1_out, _6_bit_Op[4], not_1_out, _6_bit_Op[1]);
  and and_2 (and_2_out, _6_bit_Op[4], not_2_out, _6_bit_Op[2]);
  and and_3 (Jump, not_3_out, _6_bit_Op[3], _6_bit_Op[2], _6_bit_Op[1], _6_bit_Op[0]);
  or or_1 (Branch, and_1_out, and_2_out);

  // Other names for the same wires on the sheet: Op0 = _6_bit_Op[0]; Op1 = _6_bit_Op[1]; Op2 = _6_bit_Op[2];
  //   Op3 = _6_bit_Op[3]; Op4 = _6_bit_Op[4]
endmodule
