// Logisim project PC Control.circ as structural Verilog: 3 circuits, main circuit Pc Control Unit
// Pc Control
module Pc_Control_Unit (
  input  [5:0] in_1,
  output out_2,
  output out_3,
  output [1:0] out_4
);

  J_Branch j_branch_1 (._6_bit_Op(in_1), .Branch(out_2), .Jump(out_3));
  Pc_Src pc_src_1 (._6_bit_Op(in_1), .PC_Src0(out_4[0]), .Pc_Src1(out_4[1]));
endmodule

module J_Branch (
  input  [5:0] _6_bit_Op,
  output Branch,
  output Jump
);

  wire and_1_out, and_2_out, not_1_out, not_2_out, not_3_out;

  not not_1 (not_1_out, _6_bit_Op[3]);
  not not_2 (not_2_out, _6_bit_Op[3]);
  not not_3 (not_3_out, _6_bit_Op[4]);
  and and_1 (and_1_out, _6_bit_Op[4], not_1_out, _6_bit_Op[1]);
  and and_2 (and_2_out, _6_bit_Op[4], not_2_out, _6_bit_Op[2]);
  and and_3 (Jump, not_3_out, _6_bit_Op[3], _6_bit_Op[2], _6_bit_Op[1], _6_bit_Op[0]);
  or or_1 (Branch, and_1_out, and_2_out);

  // Other names for the same wires on the sheet: Op0 = _6_bit_Op[0]; Op1 = _6_bit_Op[1]; Op2 = _6_bit_Op[2];
  //   Op3 = _6_bit_Op[3]; Op4 = _6_bit_Op[4]
endmodule

module Pc_Src (
  input  [5:0] _6_bit_Op,
  output PC_Src0,
  output Pc_Src1
);

  wire and_1_out, and_2_out, and_3_out, and_4_out, not_1_out, not_2_out, not_3_out, not_4_out, not_5_out,
       not_6_out, not_7_out, not_8_out, not_9_out, not_10_out, not_11_out;

  not not_1 (not_1_out, _6_bit_Op[4]);
  not not_2 (not_2_out, _6_bit_Op[2]);
  not not_3 (not_3_out, _6_bit_Op[4]);
  not not_4 (not_4_out, _6_bit_Op[1]);
  not not_5 (not_5_out, _6_bit_Op[4]);
  not not_6 (not_6_out, _6_bit_Op[0]);
  not not_7 (not_7_out, _6_bit_Op[3]);
  not not_8 (not_8_out, _6_bit_Op[2]);
  not not_9 (not_9_out, _6_bit_Op[1]);
  and and_1 (and_1_out, not_1_out, not_2_out);
  and and_2 (and_2_out, not_3_out, not_4_out);
  and and_3 (and_3_out, not_5_out, not_6_out);
  not not_10 (not_10_out, _6_bit_Op[3]);
  not not_11 (not_11_out, _6_bit_Op[4]);
  and and_4 (and_4_out, not_7_out, not_8_out, not_9_out);
  or or_1 (PC_Src0, and_1_out, and_2_out, and_3_out, not_10_out);
  or or_2 (Pc_Src1, not_11_out, and_4_out);

  // Other names for the same wires on the sheet: Op0 = _6_bit_Op[0]; Op1 = _6_bit_Op[1]; Op2 = _6_bit_Op[2];
  //   Op3 = _6_bit_Op[3]; Op4 = _6_bit_Op[4]
endmodule
