// Logisim project PC Unit.circ as structural Verilog: 2 circuits, main circuit Pc Unit
module Pc_Unit (
  input  [5:0] in_1,
  output out_2,
  output out_3,
  output [1:0] out_4
);

  J_Branch_control j_branch_control_1 (._6_bit_Op(in_1), .Branch(out_2), .Jump(out_3));
  PC_Src pc_src_1 (._6_bit_Op(in_1), .PC_Src0(out_4[0]), .Pc_Src1(out_4[1]));
endmodule

module d (
);

  Pc_Unit pc_unit_1 ();  // open: in_1, out_2, out_3, out_4
endmodule
