// Logisim project PC counter.circ as structural Verilog: 1 circuit, main circuit PC Counter
module PC_Counter (
  input  [4:0] in_1,
  input  [10:0] in_2,
  input  [15:0] in_3,
  input  [31:0] Rs1,
  input  Jump_Signal,
  input  Brach_Signal,
  input  clk,
  output [19:0] OutPc,
  output [19:0] OutPcPlus1
);

  wire [19:0] bit_extender_1_out, bit_extender_2_out, initial_pc, OutPcPlus1_t, Pc_JALR;

  assign bit_extender_1_out = {{4{1'b0}}, {in_2, in_1}};  // Bit_Extender bit_extender_1
  assign bit_extender_2_out = {{4{1'b0}}, in_3};  // Bit_Extender bit_extender_2
  // Register #(.width(20)) register_1: pin names not known; wires that end beside it: initial_pc, 1'b1
  Adder #(.width(20)) adder_1 (.a(initial_pc), .b(bit_extender_1_out), .out(OutPcPlus1_t), .cin(1'b0));  // open: cout
  Adder #(.width(20)) adder_2 (.a(bit_extender_2_out), .b(Rs1[19:0]), .out(Pc_JALR), .cin(1'b0));  // open: cout
  Adder #(.width(20)) adder_3 (.a(OutPc), .b(20'h1), .out(OutPcPlus1), .cin(1'b0));  // open: cout
  Multiplexer #(.select(2), .width(20), .enable("false")) multiplexer_1 (
    .in0(OutPcPlus1_t), .in1(OutPcPlus1_t), .in2(Pc_JALR), .out(initial_pc), .sel({Jump_Signal, Brach_Signal}));  // open: in3

  // Other names for the same wires on the sheet: PC_branch[19:0] = OutPcPlus1_t

  // Notes on the sheet:
  //   JALR Rd,Rs1,imm16
  //   Pc
  //   PC_branch
  //   Next Pc
endmodule
