// Logisim project PC counter2.circ as structural Verilog: 5 circuits, main circuit main
module main (
  input  [4:0] in_1,
  input  [10:0] in_2,
  input  [15:0] in_3,
  input  [31:0] Rs1,
  input  Jump_Signal,
  input  Brach_Signal,
  input  clk,
  output [19:0] OutPc,
  output [19:0] OutPcPlus1
);

  wire [19:0] bit_extender_1_out, bit_extender_2_out, initial_pc, OutPcPlus1_t, Pc_JALR;

  assign bit_extender_1_out = {{4{1'b0}}, {in_2, in_1}};  // Bit_Extender bit_extender_1
  assign bit_extender_2_out = {{4{1'b0}}, in_3};  // Bit_Extender bit_extender_2
  Register #(.width(20)) register_1 (.D(initial_pc), .en(1'b1), .Q(OutPc), .clk(clk));  // open: clr
  Adder #(.width(20)) adder_1 (.a(initial_pc), .b(bit_extender_1_out), .out(OutPcPlus1_t), .cin(1'b0));  // open: cout
  Adder #(.width(20)) adder_2 (.a(bit_extender_2_out), .b(Rs1[19:0]), .out(Pc_JALR), .cin(1'b0));  // open: cout
  Adder #(.width(20)) adder_3 (.a(OutPc), .b(20'h1), .out(OutPcPlus1), .cin(1'b0));  // open: cout
  Multiplexer #(.select(2), .width(20), .enable("false")) multiplexer_1 (
    .in0(OutPcPlus1_t), .in1(OutPcPlus1_t), .in2(Pc_JALR), .out(initial_pc), .sel({Jump_Signal, Brach_Signal}));  // open: in3

  // Other names for the same wires on the sheet: PC_branch[19:0] = OutPcPlus1_t

  // Notes on the sheet:
  //   JALR Rd,Rs1,imm16
  //   Pc
  //   PC_branch
  //   Next Pc
endmodule

module PC_1 (
  input  [19:0] Initial_Pc,
  output [19:0] OutPcPlus1
);

  Adder #(.width(20)) adder_1 (.a(Initial_Pc), .b(20'h1), .out(OutPcPlus1), .cin(1'b0));  // open: cout
endmodule

module Jump (
  input  [19:0] initial_pc,
  input  [15:0] Imm16,
  input  [31:0] Rs1,
  output [19:0] Pc_jump
);

  wire [19:0] bit_extender_1_out;

  assign bit_extender_1_out = {{4{1'b0}}, Imm16};  // Bit_Extender bit_extender_1
  Adder #(.width(20)) adder_1 (.a(bit_extender_1_out), .b(Rs1[19:0]), .out(Pc_jump), .cin(1'b0));  // open: cout

  // Notes on the sheet:
  //   JALR Rd,Rs1,imm16
endmodule

module Branch_pc (
  input  [4:0] ImmL,
  input  [10:0] ImmU,
  input  [19:0] initial_pc,
  input  Zero_flag,
  input  Slt,
  input  SltU,
  output [19:0] Pc_Branch
);

  wire [19:0] bit_extender_1_out;

  assign bit_extender_1_out = {{4{1'b0}}, {ImmU, ImmL}};  // Bit_Extender bit_extender_1
  Adder #(.width(20)) adder_1 (.a(initial_pc), .b(bit_extender_1_out), .out(Pc_Branch), .cin(1'b0));  // open: cout
endmodule

module PC_Selection (
  input  [19:0] Pc_1,
  input  [19:0] PC_branch,
  input  [19:0] Pc_jump,
  input  Jump_Signal,
  input  Brach_Signal,
  output [19:0] initial_pc
);

  Multiplexer #(.select(2), .width(20), .enable("false")) multiplexer_1 (
    .in0(Pc_1), .in1(Pc_1), .in2(Pc_jump), .out(initial_pc), .sel({Jump_Signal, Brach_Signal}));  // open: in3

  assign PC_branch = Pc_1;
endmodule
