// Logisim project Pipeline_Processor.circ as structural Verilog: 7 circuits, main circuit Pipline_Processor
module Pipline_Processor (
);

  wire alu_1_p5, ALUSrc, ALUSrc_EX, ALUSrc_ID, B_EX, button_1_out, clock_1_out, Ext, Ext_ID, ImmSelect,
       ImmSelect_ID, J, J_controlUnit, J_ID, Kill_1, Kill_2, MemRd, MemRd_EX, MemRd_ID, MemRd_MEM, MemWr,
       MemWr_EX, MemWr_ID, MemWr_MEM, or_3_out, RegSource, RegSource_ID, RegWr, RegWr_EX, RegWr_ID,
       RegWr_MEM, RegWr_WB, Stall;
  wire [1:0] ForwardA, ForwardB, MemtoReg, MemtoReg_EX, MemtoReg_ID, MemtoReg_MEM, MemtoReg_WB, or_2_out;
  wire [4:0] ImmL, instruction_spliter_1_rs1, Rd_EX, Rd_ID, Rd_MEM, Rd_WB, Rs, Rt;
  wire [5:0] OpCode;
  wire [10:0] Function, ImmU;
  wire [12:0] ALU_Control_EX, ALU_Control_ID;
  wire [15:0] Imm16_EX, Imm16_ID;
  wire [19:0] BranshPC_EX, BranshPC_ID, JumpPC, multiplexer_1_out, PC_1, PC_ID, PC_IF;
  wire [31:0] ALU_Forward, data_memory_1_data_out, ex_mem_1_out_10, ex_mem_1_out_12, Ext_PC_EX, Ext_PC_ID,
       Ext_PC_MEM, Extended_EX, Extended_ID, id_ex_1_out_19, Inst_ID,
       instruction_memory_1__32_bit_iinstruction, MEM_Forward, multiplexer_2_out, multiplexer_4_out,
       multiplexer_5_out, multiplexer_7_out, Output_WB, R0, R1, R2, R3, R4, R5, R6, R7, R8, R9, R10, R11,
       R12, R13, R14, R15, R16, R17, R18, R19, R20, R21, R22, R23, R24, R25, R26, R27, R28, R29, R30, R31,
       Rs1, Rs2_EX, Rs2_ID;

  Multiplexer #(.select(2), .width(20), .enable("false")) multiplexer_1 (
    .in0(PC_1), .in1(BranshPC_EX), .in2(JumpPC), .in3(PC_IF), .out(multiplexer_1_out), .sel(or_2_out));
  or or_1 (or_2_out[1], J, Stall);
  or or_2 (or_2_out[0], Stall, B_EX);
  PC_control pc_control_1 (.J(J_ID), .B(B_EX), .Jump(J), .Kill1(Kill_1), .Kill2(Kill_2));
  PC_1 pc_1_1 (.Initial_Pc(PC_IF), .OutPcPlus1(PC_1));
  Register #(.width(20)) Register (.D(multiplexer_1_out), .en(1'b1), .Q(PC_IF), .clk(clock_1_out), .clr(button_1_out));
  Button button_1 (.out(button_1_out));
  Jump jump_1 (.Imm16(Imm16_ID), .Rs1(Rs1), .Pc_jump(JumpPC), .initial_pc(PC_ID));
  Instruction_Memory instruction_memory_1 (
    .PC(PC_IF), ._32_bit_iinstruction(instruction_memory_1__32_bit_iinstruction));
  // Probe on JumpPC
  // Probe on instruction_memory_1__32_bit_iinstruction
  // Probe on R0
  // Probe on R1
  // Probe on R2
  // Probe on R3
  // Probe on R4
  // Probe on R5
  // Probe on R6
  // Probe on R7
  IF_ID_Registers if_id_registers_1 (
    .Pc_1(PC_IF), .CLK(clock_1_out), .in_2(multiplexer_2_out), .out_4(PC_ID), .out_5(Inst_ID));
  Multiplexer #(.select(2), .width(32), .enable("false")) multiplexer_2 (
    .in0(instruction_memory_1__32_bit_iinstruction), .in1({32{1'b0}}), .in2(Inst_ID),
    .out(multiplexer_2_out), .sel({Stall, Kill_1}));  // open: in3
  // Probe on Inst_ID
  // Probe on R8
  // Probe on R9
  // Probe on R10
  // Probe on R11
  // Probe on R12
  // Probe on R13
  // Probe on R14
  // Probe on R15
  Instruction_Spliter instruction_spliter_1 (
    .in_1(Inst_ID), .Opcode(OpCode), .RD(Rd_ID), .ImmL(ImmL), .Rs1(instruction_spliter_1_rs1), .Rs2(Rt),
    .ImmU(ImmU), .F(Function), .Imm16(Imm16_ID));
  // Probe on Function
  // Probe on B_EX
  // Probe on instruction_spliter_1_rs1
  // Probe on Rd_ID
  // Probe on OpCode
  Control_Signal_Unit control_signal_unit_1 (
    .OP6(OpCode), .out_4(RegWr), .out_5(MemRd), .out_6(MemWr), .out_7(MemtoReg), .out_8(Ext), .out_9(ALUSrc),
    .out_10(ImmSelect), .out_3(RegSource), .Jump(J_controlUnit));
  // Probe on PC_IF
  Multiplexer #(.width(5), .enable("false")) multiplexer_3 (
    .in0(instruction_spliter_1_rs1), .in1(Rd_ID), .out(Rs), .sel(RegSource_ID));
  // Probe on Rt
  // Probe on Rd_WB
  // Probe on R16
  // Probe on R17
  // Probe on R18
  // Probe on R19
  // Probe on R20
  // Probe on R21
  // Probe on R22
  // Probe on R23
  Clock clock_1 (.out(clock_1_out));
  // Probe on J
  // Probe on R24
  // Probe on R25
  // Probe on R26
  // Probe on R27
  // Probe on R28
  // Probe on R29
  // Probe on R30
  // Probe on R31
  Register_File register_file_1 (
    .BusW(Output_WB), .RegWrite(RegWr_WB), .R2(R2), .R3(R3), .R4(R4), .R5(R5), .R6(R6), .R7(R7), .R8(R8),
    .R9(R9), .R10(R10), .R11(R11), .R12(R12), .R14(R14), .R15(R15), .R16(R16), .R17(R17), .R18(R18),
    .R19(R19), .R20(R20), .R21(R21), .R22(R22), .R23(R23), .R24(R24), .R25(R25), .R26(R26), .R27(R27),
    .R28(R28), .R29(R29), .R30(R30), .R31(R31), .BusA(Rs1), .BusB(Rs2_ID), .R1(R1), .R13(R13), .Rs1(Rs),
    .Rs2(Rt), .Clock(clock_1_out), .Rd(Rd_WB), .R0(R0));
  Branch_pc branch_pc_1 (.ImmL(ImmL), .ImmU(ImmU), .initial_pc(PC_ID), .Pc_Branch(BranshPC_ID));
  ALU_Control alu_control_1 (.ALU_Control(ALU_Control_ID), .Opcode(OpCode), .Function(Function));
  Extender extender_1 (
    .Extender_Op(Ext_ID), .Immediate(Extended_ID), .Imm16(Imm16_ID), .ImmSelect(ImmSelect_ID), .ImmU(ImmU),
    .ImmL(ImmL), .PC_1(PC_ID), .PC_Extended(Ext_PC_ID));
  // Probe on Rs1
  // Probe on Rs2_ID
  // Hazard_Detect_Forward_and_Stall hazard_detect_forward_and_stall_1: pin names not known; wires that end beside it: Rs, Rt, Rd_EX, Rd_MEM, Rd_WB, RegWr_EX, RegWr_MEM, RegWr_WB, MemRd_EX, ForwardA, ForwardB, Stall
  // Probe on ForwardA
  Multiplexer #(.select(2), .width(32), .enable("false")) multiplexer_4 (
    .in0(Rs1), .in1(ALU_Forward), .in2(MEM_Forward), .in3(Output_WB), .out(multiplexer_4_out), .sel(ForwardA));
  Multiplexer #(.select(2), .width(32), .enable("false")) multiplexer_5 (
    .in0(Rs2_ID), .in1(ALU_Forward), .in2(MEM_Forward), .in3(Output_WB), .out(multiplexer_5_out),
    .sel(ForwardB));
  // Probe on ForwardB
  // Probe on multiplexer_4_out
  // Probe on multiplexer_5_out
  or or_3 (or_3_out, Kill_2, Stall);
  Multiplexer #(.width(10), .enable("false")) multiplexer_6 (
    .in0({ImmSelect, Ext, MemtoReg, MemWr, MemRd, ALUSrc, RegWr, RegSource, J_controlUnit}),
    .in1({10{1'b0}}),
    .out({ImmSelect_ID, Ext_ID, MemtoReg_ID, MemWr_ID, MemRd_ID, ALUSrc_ID, RegWr_ID, RegSource_ID, J_ID}),
    .sel(or_3_out));
  // Probe on BranshPC_EX
  ID_EX id_ex_1 (
    .in_1(BranshPC_ID), .in_3(Imm16_ID), .in_5(multiplexer_4_out), .in_7(multiplexer_5_out),
    .out_15(BranshPC_EX), .out_17(Imm16_EX), .out_19(id_ex_1_out_19), .out_21(Rs2_EX), .in_13(Rd_ID),
    .out_27(Rd_EX), .in_14(clock_1_out), .in_2(ALUSrc_ID), .out_16(ALUSrc_EX), .in_4(ALU_Control_ID),
    .out_18(ALU_Control_EX), .in_6(MemRd_ID), .out_20(MemRd_EX), .in_8(MemWr_ID), .out_22(MemWr_EX),
    .in_10(MemtoReg_ID), .out_24(MemtoReg_EX), .in_12(RegWr_ID), .out_26(RegWr_EX), .in_9(Ext_PC_ID),
    .out_23(Ext_PC_EX), .in_11(Extended_ID), .out_25(Extended_EX));
  // Probe on id_ex_1_out_19
  // Probe on multiplexer_7_out
  Multiplexer #(.width(32), .enable("false")) multiplexer_7 (
    .in0(Rs2_EX), .in1(Extended_EX), .out(multiplexer_7_out), .sel(ALUSrc_EX));
  // ALU alu_1: pin names not known; wires that end beside it: id_ex_1_out_19, multiplexer_7_out, B_EX, ALU_Control_EX, alu_1_p5, alu_1_p5, ALU_Forward
  // Probe on ALU_Forward
  EX_MEM ex_mem_1 (
    .in_1(ALU_Forward), .in_3(Rs2_EX), .in_7(Rd_EX), .out_10(ex_mem_1_out_10), .out_12(ex_mem_1_out_12),
    .out_16(Rd_MEM), .in_2(MemRd_EX), .out_11(MemRd_MEM), .in_4(MemWr_EX), .out_13(MemWr_MEM),
    .in_6(MemtoReg_EX), .out_15(MemtoReg_MEM), .in_8(RegWr_EX), .out_17(RegWr_MEM), .in_5(Ext_PC_EX),
    .out_14(Ext_PC_MEM), .in_9(clock_1_out));
  // Probe on ex_mem_1_out_10
  Data_Memory data_memory_1 (
    .Address(ex_mem_1_out_10), .Data_In(ex_mem_1_out_12), .Memory_Write(MemWr_MEM), .Clock(clock_1_out),
    .Data_Out(data_memory_1_data_out), .Memory_Read(MemRd_MEM));
  Multiplexer #(.select(2), .width(32), .enable("false")) multiplexer_8 (
    .in0(ex_mem_1_out_10), .in1(data_memory_1_data_out), .in2(Ext_PC_MEM), .out(MEM_Forward),
    .sel(MemtoReg_MEM));  // open: in3
  // Probe on MEM_Forward
  MEM_WB mem_wb_1 (
    .in_2(MEM_Forward), .in_4(Rd_MEM), .out_7(Output_WB), .out_9(Rd_WB), .in_1(MemtoReg_MEM),
    .out_6(MemtoReg_WB), .in_3(RegWr_MEM), .out_8(RegWr_WB), .CLk(clock_1_out));
  // Probe on Output_WB
endmodule

module Instruction_Spliter (
  input  [31:0] in_1,
  output [5:0] Opcode,
  output [4:0] RD,
  output [4:0] ImmL,
  output [4:0] Rs1,
  output [15:0] Imm16,
  output [10:0] F,
  output [10:0] ImmU,
  output [4:0] Rs2
);


  assign F = in_1[31:21];
  assign Imm16 = in_1[31:16];
  assign ImmL = in_1[10:6];
  assign ImmU = in_1[31:21];
  assign Opcode = in_1[5:0];
  assign RD = in_1[10:6];
  assign Rs1 = in_1[15:11];
  assign Rs2 = in_1[20:16];

  // Notes on the sheet:
  //   SB_Type
  //   R_Tube
  //   I-Type
endmodule

module IF_ID_Registers (
  input  [19:0] Pc_1,
  input  [31:0] in_2,
  input  CLK,
  output [19:0] out_4,
  output [31:0] out_5
);

  Register #(.width(20)) Next_PC (.D(Pc_1), .en(1'b1), .Q(out_4), .clk(CLK));  // open: clr
  Register #(.width(32)) Instruction_Word (.D(in_2), .en(1'b1), .Q(out_5), .clk(CLK));  // open: clr
endmodule

module ID_EX (
  input  [19:0] in_1,
  input  in_2,
  input  [15:0] in_3,
  input  [12:0] in_4,
  input  [31:0] in_5,
  input  in_6,
  input  [31:0] in_7,
  input  in_8,
  input  [31:0] in_9,
  input  [1:0] in_10,
  input  [31:0] in_11,
  input  in_12,
  input  [4:0] in_13,
  input  in_14,
  output [19:0] out_15,
  output out_16,
  output [15:0] out_17,
  output [12:0] out_18,
  output [31:0] out_19,
  output out_20,
  output [31:0] out_21,
  output out_22,
  output [31:0] out_23,
  output [1:0] out_24,
  output [31:0] out_25,
  output out_26,
  output [4:0] out_27
);

  Register #(.width(20)) Branch_PC (.D(in_1), .en(1'b1), .Q(out_15), .clk(in_14));  // open: clr
  Register #(.width(16)) Imm16 (.D(in_3), .en(1'b1), .Q(out_17), .clk(in_14));  // open: clr
  Register #(.width(32)) BusA (.D(in_5), .en(1'b1), .Q(out_19), .clk(in_14));  // open: clr
  Register #(.width(32)) BusB (.D(in_7), .en(1'b1), .Q(out_21), .clk(in_14));  // open: clr
  Register #(.width(32)) Ext_PC (.D(in_9), .en(1'b1), .Q(out_23), .clk(in_14));  // open: clr
  Register #(.width(32)) Extended (.D(in_11), .en(1'b1), .Q(out_25), .clk(in_14));  // open: clr
  Register #(.width(5)) Rd (.D(in_13), .en(1'b1), .Q(out_27), .clk(in_14));  // open: clr
  Register #(.width(1)) Alu_Src (.D(in_2), .en(1'b1), .Q(out_16), .clk(in_14));  // open: clr
  Register #(.width(13)) Alu_Control (.D(in_4), .en(1'b1), .Q(out_18), .clk(in_14));  // open: clr
  Register #(.width(1)) MemRd (.D(in_6), .en(1'b1), .Q(out_20), .clk(in_14));  // open: clr
  Register #(.width(1)) MemWr (.D(in_8), .en(1'b1), .Q(out_22), .clk(in_14));  // open: clr
  Register #(.width(2)) MemtoReg (.D(in_10), .en(1'b1), .Q(out_24), .clk(in_14));  // open: clr
  Register #(.width(1)) RegWr (.D(in_12), .en(1'b1), .Q(out_26), .clk(in_14));  // open: clr

  // Notes on the sheet:
  //   Signals
endmodule

module EX_MEM (
  input  [31:0] in_1,
  input  in_2,
  input  [31:0] in_3,
  input  in_4,
  input  [31:0] in_5,
  input  [1:0] in_6,
  input  [4:0] in_7,
  input  in_8,
  input  in_9,
  output [31:0] out_10,
  output out_11,
  output [31:0] out_12,
  output out_13,
  output [31:0] out_14,
  output [1:0] out_15,
  output [4:0] out_16,
  output out_17
);

  Register #(.width(32)) ALU_Out (.D(in_1), .en(1'b1), .Q(out_10), .clk(in_9));  // open: clr
  Register #(.width(32)) Rt (.D(in_3), .en(1'b1), .Q(out_12), .clk(in_9));  // open: clr
  Register #(.width(32)) Ext_PC (.D(in_5), .en(1'b1), .Q(out_14), .clk(in_9));  // open: clr
  Register #(.width(5)) Rd (.D(in_7), .en(1'b1), .Q(out_16), .clk(in_9));  // open: clr
  Register #(.width(1)) MemRd (.D(in_2), .en(1'b1), .Q(out_11), .clk(in_9));  // open: clr
  Register #(.width(1)) MemWr (.D(in_4), .en(1'b1), .Q(out_13), .clk(in_9));  // open: clr
  Register #(.width(2)) MemToReg (.D(in_6), .en(1'b1), .Q(out_15), .clk(in_9));  // open: clr
  Register #(.width(1)) RegWr (.D(in_8), .en(1'b1), .Q(out_17), .clk(in_9));  // open: clr

  // Notes on the sheet:
  //   Signals
endmodule

module MEM_WB (
  input  [1:0] in_1,
  input  [31:0] in_2,
  input  in_3,
  input  [4:0] in_4,
  input  CLk,
  output [1:0] out_6,
  output [31:0] out_7,
  output out_8,
  output [4:0] out_9
);

  Register #(.width(32)) WB (.D(in_2), .en(1'b1), .Q(out_7), .clk(CLk));  // open: clr
  Register #(.width(5)) Rd (.D(in_4), .en(1'b1), .Q(out_9), .clk(CLk));  // open: clr
  Register #(.width(2)) MemToReg (.D(in_1), .en(1'b1), .Q(out_6), .clk(CLk));  // open: clr
  Register #(.width(1)) RegWr (.D(in_3), .en(1'b1), .Q(out_8), .clk(CLk));  // open: clr

  // Notes on the sheet:
  //   Signals
endmodule

module PC_control (
  input  J,
  input  B,
  output Jump,
  output Kill1,
  output Kill2
);

  wire not_1_out;

  not not_1 (not_1_out, B);
  and and_1 (Jump, J, not_1_out);
  or or_1 (Kill1, Jump, B);

  assign Kill2 = B;
endmodule
