// Logisim project Hazard Detect Forward and Stall.circ as structural Verilog: 1 circuit, main circuit Hazard Detect Forward and Stall
module Hazard_Detect_Forward_and_Stall (
  input  [4:0] Rs,
  input  [4:0] Rd_EX,
  input  RegWr_EX,
  input  [4:0] Rd_MEM,
  input  RegWr_MEM,
  input  [4:0] Rd_WB,
  input  RegWr_WB,
  input  [4:0] Rt,
  input  MemRd_EX,
  input  [5:0] OpCode,
  output [1:0] ForwardA,
  output [1:0] ForwardB,
  output Stall
);

  wire and_1_out, and_2_out, and_3_out, and_4_out, and_5_out, and_6_out, and_7_out, and_8_out, and_9_out,
       and_10_out, and_11_out, and_12_out, and_13_out, and_14_out, and_15_out, and_16_out, and_17_out,
       and_18_out, and_19_out, comparator_1_eq, comparator_2_eq, comparator_3_eq, comparator_4_eq,
       comparator_5_eq, comparator_6_eq, comparator_7_eq, comparator_8_eq, Imm, not_1_out, not_2_out,
       not_3_out, not_4_out, not_5_out, not_6_out, not_7_out, not_8_out, not_9_out, not_10_out, not_11_out,
       not_12_out, not_13_out, not_14_out, not_15_out, not_16_out, not_17_out, not_18_out, not_19_out,
       not_20_out, not_21_out, not_22_out, not_23_out, not_24_out, not_25_out, not_26_out, not_27_out,
       or_6_out;
  wire [4:0] multiplexer_1_out;

  Multiplexer #(.width(5), .enable("false")) multiplexer_1 (
    .in0(Rt), .in1({5{1'b0}}), .out(multiplexer_1_out), .sel(Imm));
  Comparator #(.width(5)) comparator_1 (.a(Rs), .b({5{1'b0}}), .eq(comparator_1_eq));  // open: gt, lt
  not not_1 (not_1_out, comparator_1_eq);
  Comparator #(.width(5)) comparator_2 (.a(Rs), .b(Rd_EX), .eq(comparator_2_eq));  // open: gt, lt
  Comparator #(.width(5)) comparator_3 (.a(Rs), .b(Rd_MEM), .eq(comparator_3_eq));  // open: gt, lt
  Comparator #(.width(5)) comparator_4 (.a(Rs), .b(Rd_WB), .eq(comparator_4_eq));  // open: gt, lt
  Comparator #(.width(5)) comparator_5 (.a(multiplexer_1_out), .b({5{1'b0}}), .eq(comparator_5_eq));  // open: gt, lt
  not not_2 (not_2_out, comparator_5_eq);
  Comparator #(.width(5)) comparator_6 (.a(multiplexer_1_out), .b(Rd_EX), .eq(comparator_6_eq));  // open: gt, lt
  Comparator #(.width(5)) comparator_7 (.a(multiplexer_1_out), .b(Rd_MEM), .eq(comparator_7_eq));  // open: gt, lt
  Comparator #(.width(5)) comparator_8 (.a(multiplexer_1_out), .b(Rd_WB), .eq(comparator_8_eq));  // open: gt, lt
  not not_3 (not_3_out, OpCode[5]);
  not not_4 (not_4_out, OpCode[4]);
  not not_5 (not_5_out, OpCode[5]);
  not not_6 (not_6_out, OpCode[4]);
  not not_7 (not_7_out, OpCode[5]);
  not not_8 (not_8_out, OpCode[4]);
  not not_9 (not_9_out, OpCode[5]);
  not not_10 (not_10_out, OpCode[4]);
  not not_11 (not_11_out, OpCode[5]);
  not not_12 (not_12_out, OpCode[3]);
  not not_13 (not_13_out, OpCode[2]);
  not not_14 (not_14_out, OpCode[1]);
  not not_15 (not_15_out, OpCode[0]);
  and and_1 (and_1_out, comparator_2_eq, not_1_out, RegWr_EX);
  and and_2 (and_2_out, comparator_3_eq, not_1_out, RegWr_MEM);
  and and_3 (and_3_out, comparator_4_eq, not_1_out, RegWr_WB);
  and and_4 (and_4_out, comparator_6_eq, not_2_out, RegWr_EX);
  and and_5 (and_5_out, comparator_7_eq, not_2_out, RegWr_MEM);
  and and_6 (and_6_out, comparator_8_eq, not_2_out, RegWr_WB);
  and and_7 (and_7_out, not_3_out, not_4_out, OpCode[0]);
  and and_8 (and_8_out, not_5_out, not_6_out, OpCode[1]);
  and and_9 (and_9_out, not_7_out, not_8_out, OpCode[2]);
  and and_10 (and_10_out, not_9_out, not_10_out, OpCode[3]);
  and and_11 (and_11_out, not_11_out, OpCode[4], not_12_out, not_13_out, not_14_out, not_15_out);
  not not_16 (not_16_out, and_1_out);
  not not_17 (not_17_out, and_2_out);
  not not_18 (not_18_out, and_1_out);
  not not_19 (not_19_out, and_1_out);
  not not_20 (not_20_out, and_2_out);
  not not_21 (not_21_out, and_4_out);
  not not_22 (not_22_out, and_5_out);
  not not_23 (not_23_out, and_4_out);
  not not_24 (not_24_out, and_4_out);
  not not_25 (not_25_out, and_5_out);
  or or_1 (Imm, and_7_out, and_8_out, and_9_out, and_10_out, and_11_out);
  and and_12 (and_12_out, not_16_out, not_17_out, and_3_out);
  and and_13 (and_13_out, not_18_out, and_2_out);
  and and_14 (and_14_out, not_19_out, not_20_out, and_3_out);
  and and_15 (and_15_out, not_21_out, not_22_out, and_6_out);
  and and_16 (and_16_out, not_23_out, and_5_out);
  and and_17 (and_17_out, not_24_out, not_25_out, and_6_out);
  or or_2 (ForwardA[0], and_1_out, and_12_out);
  or or_3 (ForwardA[1], and_13_out, and_14_out);
  or or_4 (ForwardB[0], and_4_out, and_15_out);
  or or_5 (ForwardB[1], and_16_out, and_17_out);
  and and_18 (and_18_out, ForwardB[0], not_26_out);
  not not_26 (not_26_out, ForwardB[1]);
  and and_19 (and_19_out, ForwardA[0], not_27_out);
  not not_27 (not_27_out, ForwardA[1]);
  or or_6 (or_6_out, and_18_out, and_19_out);
  and and_20 (Stall, or_6_out, MemRd_EX);
endmodule
