// Logisim project Extender.circ as structural Verilog: 1 circuit, main circuit Extender
module Extender (
  input  [19:0] PC_1,
  input  [15:0] Imm16,
  input  [4:0] ImmL,
  input  Extender_Op,
  input  ImmSelect,
  input  [10:0] ImmU,
  output [31:0] PC_Extended,
  output [31:0] Immediate
);

  wire [15:0] multiplexer_1_out;
  wire [19:0] adder_1_out;
  wire [31:0] bit_extender_2_out, bit_extender_3_out;

  Adder #(.width(20)) adder_1 (.a(PC_1), .b(20'h1), .out(adder_1_out));  // open: cin, cout
  Multiplexer #(.width(16)) multiplexer_1 (
    .in0(Imm16), .in1({ImmU, ImmL}), .out(multiplexer_1_out), .sel(ImmSelect));  // open: en
  assign PC_Extended = {{12{1'b0}}, adder_1_out};  // Bit_Extender bit_extender_1
  assign bit_extender_2_out = {{16{1'b0}}, multiplexer_1_out};  // Bit_Extender bit_extender_2
  assign bit_extender_3_out = {{16{multiplexer_1_out[15]}}, multiplexer_1_out};  // Bit_Extender bit_extender_3
  Multiplexer #(.width(32)) multiplexer_2 (
    .in0(bit_extender_2_out), .in1(bit_extender_3_out), .out(Immediate), .sel(Extender_Op));  // open: en
endmodule
