// Logisim project Op_Control.circ as structural Verilog: 1 circuit, main circuit Op_Control
// Op Unit
module Op_Control (
  input  [5:0] _6_bit_Op,
  output ExtOp,
  output ALUSrc
);

  wire and_1_out, and_2_out, and_3_out, and_4_out, and_5_out, and_6_out, and_7_out, and_8_out, and_9_out,
       and_10_out, not_1_out, not_2_out, not_3_out, not_4_out, not_5_out, not_6_out, not_7_out, not_8_out,
       not_9_out, not_10_out, not_11_out, not_12_out, not_13_out, not_14_out, not_15_out;

  not not_1 (not_1_out, _6_bit_Op[4]);
  not not_2 (not_2_out, _6_bit_Op[2]);
  not not_3 (not_3_out, _6_bit_Op[1]);
  not not_4 (not_4_out, _6_bit_Op[0]);
  not not_5 (not_5_out, _6_bit_Op[4]);
  not not_6 (not_6_out, _6_bit_Op[1]);
  not not_7 (not_7_out, _6_bit_Op[4]);
  not not_8 (not_8_out, _6_bit_Op[0]);
  not not_9 (not_9_out, _6_bit_Op[4]);
  not not_10 (not_10_out, _6_bit_Op[3]);
  not not_11 (not_11_out, _6_bit_Op[3]);
  not not_12 (not_12_out, _6_bit_Op[3]);
  not not_13 (not_13_out, _6_bit_Op[3]);
  not not_14 (not_14_out, _6_bit_Op[4]);
  not not_15 (not_15_out, _6_bit_Op[3]);
  and and_1 (and_1_out, not_1_out, not_2_out, not_3_out, not_4_out);
  and and_2 (and_2_out, not_5_out, _6_bit_Op[2], not_6_out, _6_bit_Op[0]);
  and and_3 (and_3_out, not_7_out, _6_bit_Op[2], _6_bit_Op[1], not_8_out);
  and and_4 (and_4_out, not_9_out, _6_bit_Op[3], _6_bit_Op[2], _6_bit_Op[1]);
  and and_5 (and_5_out, _6_bit_Op[4], not_10_out);
  and and_6 (and_6_out, not_11_out, _6_bit_Op[0]);
  and and_7 (and_7_out, not_12_out, _6_bit_Op[1]);
  and and_8 (and_8_out, not_13_out, _6_bit_Op[2]);
  and and_9 (and_9_out, not_14_out, _6_bit_Op[3]);
  and and_10 (and_10_out, _6_bit_Op[4], not_15_out);
  or or_1 (ExtOp, and_1_out, and_2_out, and_3_out, and_4_out, and_5_out);
  or or_2 (ALUSrc, and_6_out, and_7_out, and_8_out, and_9_out, and_10_out);

  // Other names for the same wires on the sheet: Op0 = _6_bit_Op[0]; Op1 = _6_bit_Op[1]; Op2 = _6_bit_Op[2];
  //   Op3 = _6_bit_Op[3]; Op4 = _6_bit_Op[4]
endmodule
