// Logisim project Register_File.circ as structural Verilog: 1 circuit, main circuit Register File
module Register_File (
  input  [4:0] Rs1,
  input  [4:0] Rs2,
  input  [4:0] Rd,
  input  [31:0] BusW,
  input  RegWrite,
  input  Clock,
  output [31:0] R1,
  output [31:0] R2,
  output [31:0] R3,
  output [31:0] R4,
  output [31:0] R5,
  output [31:0] R6,
  output [31:0] R7,
  output [31:0] R8,
  output [31:0] R9,
  output [31:0] R10,
  output [31:0] R11,
  output [31:0] R12,
  output [31:0] R13,
  output [31:0] R14,
  output [31:0] R15,
  output [31:0] R16,
  output [31:0] R17,
  output [31:0] R18,
  output [31:0] R19,
  output [31:0] R20,
  output [31:0] R21,
  output [31:0] R22,
  output [31:0] R23,
  output [31:0] R24,
  output [31:0] R25,
  output [31:0] R26,
  output [31:0] R27,
  output [31:0] R28,
  output [31:0] R29,
  output [31:0] R30,
  output [31:0] R31,
  output [31:0] BusA,
  output [31:0] BusB
);

  wire and_1_out, and_2_out, and_3_out, and_4_out, and_5_out, and_6_out, and_7_out, and_8_out, and_9_out,
       and_10_out, and_11_out, and_12_out, and_13_out, and_14_out, and_15_out, and_16_out, and_17_out,
       and_18_out, and_19_out, and_20_out, and_21_out, and_22_out, and_23_out, and_24_out, and_25_out,
       and_26_out, and_27_out, and_28_out, and_29_out, and_30_out, and_31_out, BA0, BA1, BA2, BA3, BA4, BA5,
       BA6, BA7, BA8, BA9, BA10, BA11, BA12, BA13, BA14, BA16, BA17, BA18, BA19, BA20, BA21, BA22, BA23,
       BA24, BA25, BA26, BA27, BA28, BA29, BA30, BA31, BB0, BB1, BB2, BB3, BB4, BB5, BB6, BB7, BB8, BB9,
       BB10, BB11, BB12, BB13, BB14, BB16, BB17, BB18, BB19, BB20, BB21, BB22, BB23, BB24, BB25, BB26, BB27,
       BB28, BB29, BB30, BB31, R1_t, R2_t, R3_t, R4_t, R5_t, R6_t, R7_t, R8_t, R9_t, R10_t, R11_t, R12_t,
       R13_t, R14_t, R16_t, R17_t, R18_t, R19_t, R20_t, R21_t, R22_t, R23_t, R24_t, R25_t, R26_t, R27_t,
       R28_t, R29_t, R30_t, R31_t;

  Decoder #(.select(5), .tristate("true"), .disabled(0), .enable("false")) decoder_1 (
    .out1(R1_t), .out2(R2_t), .out3(R3_t), .out4(R4_t), .out5(R5_t), .out6(R6_t), .out7(R7_t), .out8(R8_t),
    .out9(R9_t), .out10(R10_t), .out11(R11_t), .out12(R12_t), .out13(R13_t), .out14(R14_t), .out15(R14_t),
    .out16(R16_t), .out17(R17_t), .out18(R18_t), .out19(R19_t), .out20(R20_t), .out21(R21_t), .out22(R22_t),
    .out23(R23_t), .out24(R24_t), .out25(R25_t), .out26(R26_t), .out27(R27_t), .out28(R28_t), .out29(R29_t),
    .out30(R30_t), .out31(R31_t), .sel(Rd));  // open: out0
  and and_1 (and_1_out, R1_t, RegWrite);
  and and_2 (and_2_out, R2_t, RegWrite);
  and and_3 (and_3_out, R3_t, RegWrite);
  and and_4 (and_4_out, R4_t, RegWrite);
  and and_5 (and_5_out, R5_t, RegWrite);
  and and_6 (and_6_out, R6_t, RegWrite);
  and and_7 (and_7_out, R7_t, RegWrite);
  and and_8 (and_8_out, R8_t, RegWrite);
  and and_9 (and_9_out, R9_t, RegWrite);
  and and_10 (and_10_out, R10_t, RegWrite);
  and and_11 (and_11_out, R11_t, RegWrite);
  and and_12 (and_12_out, R12_t, RegWrite);
  and and_13 (and_13_out, R13_t, RegWrite);
  and and_14 (and_14_out, R14_t, RegWrite);
  and and_15 (and_15_out, R14_t, RegWrite);
  and and_16 (and_16_out, R16_t, RegWrite);
  and and_17 (and_17_out, R17_t, RegWrite);
  and and_18 (and_18_out, R18_t, RegWrite);
  and and_19 (and_19_out, R19_t, RegWrite);
  and and_20 (and_20_out, R20_t, RegWrite);
  and and_21 (and_21_out, R21_t, RegWrite);
  and and_22 (and_22_out, R22_t, RegWrite);
  and and_23 (and_23_out, R23_t, RegWrite);
  and and_24 (and_24_out, R24_t, RegWrite);
  and and_25 (and_25_out, R25_t, RegWrite);
  and and_26 (and_26_out, R26_t, RegWrite);
  and and_27 (and_27_out, R27_t, RegWrite);
  and and_28 (and_28_out, R28_t, RegWrite);
  and and_29 (and_29_out, R29_t, RegWrite);
  and and_30 (and_30_out, R30_t, RegWrite);
  and and_31 (and_31_out, R31_t, RegWrite);
  Decoder #(.select(5), .tristate("true"), .disabled(0), .enable("false")) decoder_2 (
    .out0(BA0), .out1(BA1), .out2(BA2), .out3(BA3), .out4(BA4), .out5(BA5), .out6(BA6), .out7(BA7),
    .out8(BA8), .out9(BA9), .out10(BA10), .out11(BA11), .out12(BA12), .out13(BA13), .out14(BA14),
    .out15(BA14), .out16(BA16), .out17(BA17), .out18(BA18), .out19(BA19), .out20(BA20), .out21(BA21),
    .out22(BA22), .out23(BA23), .out24(BA24), .out25(BA25), .out26(BA26), .out27(BA27), .out28(BA28),
    .out29(BA29), .out30(BA30), .out31(BA31), .sel(Rs1));
  Register #(.width(32)) register_1 (.D(BusW), .en(and_1_out), .Q(R1), .clk(Clock));  // open: clr
  Register #(.width(32)) register_2 (.D(BusW), .en(and_2_out), .Q(R2), .clk(Clock));  // open: clr
  Register #(.width(32)) register_3 (.D(BusW), .en(and_3_out), .Q(R3), .clk(Clock));  // open: clr
  Register #(.width(32)) register_4 (.D(BusW), .en(and_4_out), .Q(R4), .clk(Clock));  // open: clr
  Register #(.width(32)) register_5 (.D(BusW), .en(and_5_out), .Q(R5), .clk(Clock));  // open: clr
  Register #(.width(32)) register_6 (.D(BusW), .en(and_6_out), .Q(R6), .clk(Clock));  // open: clr
  Register #(.width(32)) register_7 (.D(BusW), .en(and_7_out), .Q(R7), .clk(Clock));  // open: clr
  Register #(.width(32)) register_8 (.D(BusW), .en(and_8_out), .Q(R8), .clk(Clock));  // open: clr
  Register #(.width(32)) register_9 (.D(BusW), .en(and_9_out), .Q(R9), .clk(Clock));  // open: clr
  Register #(.width(32)) register_10 (.D(BusW), .en(and_10_out), .Q(R10), .clk(Clock));  // open: clr
  Register #(.width(32)) register_11 (.D(BusW), .en(and_11_out), .Q(R11), .clk(Clock));  // open: clr
  Register #(.width(32)) register_12 (.D(BusW), .en(and_12_out), .Q(R12), .clk(Clock));  // open: clr
  Register #(.width(32)) register_13 (.D(BusW), .en(and_13_out), .Q(R13), .clk(Clock));  // open: clr
  Register #(.width(32)) register_14 (.D(BusW), .en(and_14_out), .Q(R14), .clk(Clock));  // open: clr
  Register #(.width(32)) register_15 (.D(BusW), .en(and_15_out), .Q(R15), .clk(Clock));  // open: clr
  Register #(.width(32)) register_16 (.D(BusW), .en(and_16_out), .Q(R16), .clk(Clock));  // open: clr
  Register #(.width(32)) register_17 (.D(BusW), .en(and_17_out), .Q(R17), .clk(Clock));  // open: clr
  Register #(.width(32)) register_18 (.D(BusW), .en(and_18_out), .Q(R18), .clk(Clock));  // open: clr
  Register #(.width(32)) register_19 (.D(BusW), .en(and_19_out), .Q(R19), .clk(Clock));  // open: clr
  Register #(.width(32)) register_20 (.D(BusW), .en(and_20_out), .Q(R20), .clk(Clock));  // open: clr
  Register #(.width(32)) register_21 (.D(BusW), .en(and_21_out), .Q(R21), .clk(Clock));  // open: clr
  Register #(.width(32)) register_22 (.D(BusW), .en(and_22_out), .Q(R22), .clk(Clock));  // open: clr
  Register #(.width(32)) register_23 (.D(BusW), .en(and_23_out), .Q(R23), .clk(Clock));  // open: clr
  Register #(.width(32)) register_24 (.D(BusW), .en(and_24_out), .Q(R24), .clk(Clock));  // open: clr
  Register #(.width(32)) register_25 (.D(BusW), .en(and_25_out), .Q(R25), .clk(Clock));  // open: clr
  Register #(.width(32)) register_26 (.D(BusW), .en(and_26_out), .Q(R26), .clk(Clock));  // open: clr
  Register #(.width(32)) register_27 (.D(BusW), .en(and_27_out), .Q(R27), .clk(Clock));  // open: clr
  Register #(.width(32)) register_28 (.D(BusW), .en(and_28_out), .Q(R28), .clk(Clock));  // open: clr
  Register #(.width(32)) register_29 (.D(BusW), .en(and_29_out), .Q(R29), .clk(Clock));  // open: clr
  Register #(.width(32)) register_30 (.D(BusW), .en(and_30_out), .Q(R30), .clk(Clock));  // open: clr
  Register #(.width(32)) register_31 (.D(BusW), .en(and_31_out), .Q(R31), .clk(Clock));  // open: clr
  assign BusA = BA0 ? {32{1'b0}} : 32'bz;  // Controlled_Buffer controlled_buffer_1
  assign BusA = BA1 ? R1 : 32'bz;  // Controlled_Buffer controlled_buffer_2
  assign BusA = BA2 ? R2 : 32'bz;  // Controlled_Buffer controlled_buffer_3
  assign BusA = BA3 ? R3 : 32'bz;  // Controlled_Buffer controlled_buffer_4
  assign BusA = BA4 ? R4 : 32'bz;  // Controlled_Buffer controlled_buffer_5
  assign BusA = BA5 ? R5 : 32'bz;  // Controlled_Buffer controlled_buffer_6
  assign BusA = BA6 ? R6 : 32'bz;  // Controlled_Buffer controlled_buffer_7
  assign BusA = BA7 ? R7 : 32'bz;  // Controlled_Buffer controlled_buffer_8
  assign BusA = BA8 ? R8 : 32'bz;  // Controlled_Buffer controlled_buffer_9
  assign BusA = BA9 ? R9 : 32'bz;  // Controlled_Buffer controlled_buffer_10
  assign BusA = BA10 ? R10 : 32'bz;  // Controlled_Buffer controlled_buffer_11
  assign BusA = BA11 ? R11 : 32'bz;  // Controlled_Buffer controlled_buffer_12
  assign BusA = BA12 ? R12 : 32'bz;  // Controlled_Buffer controlled_buffer_13
  assign BusA = BA13 ? R13 : 32'bz;  // Controlled_Buffer controlled_buffer_14
  assign BusA = BA14 ? R14 : 32'bz;  // Controlled_Buffer controlled_buffer_15
  assign BusA = BA14 ? R15 : 32'bz;  // Controlled_Buffer controlled_buffer_16
  assign BusA = BA16 ? R16 : 32'bz;  // Controlled_Buffer controlled_buffer_17
  assign BusA = BA17 ? R17 : 32'bz;  // Controlled_Buffer controlled_buffer_18
  assign BusA = BA18 ? R18 : 32'bz;  // Controlled_Buffer controlled_buffer_19
  assign BusA = BA19 ? R19 : 32'bz;  // Controlled_Buffer controlled_buffer_20
  assign BusA = BA20 ? R20 : 32'bz;  // Controlled_Buffer controlled_buffer_21
  assign BusA = BA21 ? R21 : 32'bz;  // Controlled_Buffer controlled_buffer_22
  assign BusA = BA22 ? R22 : 32'bz;  // Controlled_Buffer controlled_buffer_23
  assign BusA = BA23 ? R23 : 32'bz;  // Controlled_Buffer controlled_buffer_24
  assign BusA = BA24 ? R24 : 32'bz;  // Controlled_Buffer controlled_buffer_25
  assign BusA = BA25 ? R25 : 32'bz;  // Controlled_Buffer controlled_buffer_26
  assign BusA = BA26 ? R26 : 32'bz;  // Controlled_Buffer controlled_buffer_27
  assign BusA = BA27 ? R27 : 32'bz;  // Controlled_Buffer controlled_buffer_28
  assign BusA = BA28 ? R28 : 32'bz;  // Controlled_Buffer controlled_buffer_29
  assign BusA = BA29 ? R29 : 32'bz;  // Controlled_Buffer controlled_buffer_30
  assign BusA = BA30 ? R30 : 32'bz;  // Controlled_Buffer controlled_buffer_31
  assign BusA = BA31 ? R31 : 32'bz;  // Controlled_Buffer controlled_buffer_32
  Decoder #(.select(5), .tristate("true"), .disabled(0), .enable("false")) decoder_3 (
    .out0(BB0), .out1(BB1), .out2(BB2), .out3(BB3), .out4(BB4), .out5(BB5), .out6(BB6), .out7(BB7),
    .out8(BB8), .out9(BB9), .out10(BB10), .out11(BB11), .out12(BB12), .out13(BB13), .out14(BB14),
    .out15(BB14), .out16(BB16), .out17(BB17), .out18(BB18), .out19(BB19), .out20(BB20), .out21(BB21),
    .out22(BB22), .out23(BB23), .out24(BB24), .out25(BB25), .out26(BB26), .out27(BB27), .out28(BB28),
    .out29(BB29), .out30(BB30), .out31(BB31), .sel(Rs2));
  assign BusB = BB0 ? {32{1'b0}} : 32'bz;  // Controlled_Buffer controlled_buffer_33
  assign BusB = BB1 ? R1 : 32'bz;  // Controlled_Buffer controlled_buffer_34
  assign BusB = BB2 ? R2 : 32'bz;  // Controlled_Buffer controlled_buffer_35
  assign BusB = BB3 ? R3 : 32'bz;  // Controlled_Buffer controlled_buffer_36
  assign BusB = BB4 ? R4 : 32'bz;  // Controlled_Buffer controlled_buffer_37
  assign BusB = BB5 ? R5 : 32'bz;  // Controlled_Buffer controlled_buffer_38
  assign BusB = BB6 ? R6 : 32'bz;  // Controlled_Buffer controlled_buffer_39
  assign BusB = BB7 ? R7 : 32'bz;  // Controlled_Buffer controlled_buffer_40
  assign BusB = BB8 ? R8 : 32'bz;  // Controlled_Buffer controlled_buffer_41
  assign BusB = BB9 ? R9 : 32'bz;  // Controlled_Buffer controlled_buffer_42
  assign BusB = BB10 ? R10 : 32'bz;  // Controlled_Buffer controlled_buffer_43
  assign BusB = BB11 ? R11 : 32'bz;  // Controlled_Buffer controlled_buffer_44
  assign BusB = BB12 ? R12 : 32'bz;  // Controlled_Buffer controlled_buffer_45
  assign BusB = BB13 ? R13 : 32'bz;  // Controlled_Buffer controlled_buffer_46
  assign BusB = BB14 ? R14 : 32'bz;  // Controlled_Buffer controlled_buffer_47
  assign BusB = BB14 ? R15 : 32'bz;  // Controlled_Buffer controlled_buffer_48
  assign BusB = BB16 ? R16 : 32'bz;  // Controlled_Buffer controlled_buffer_49
  assign BusB = BB17 ? R17 : 32'bz;  // Controlled_Buffer controlled_buffer_50
  assign BusB = BB18 ? R18 : 32'bz;  // Controlled_Buffer controlled_buffer_51
  assign BusB = BB19 ? R19 : 32'bz;  // Controlled_Buffer controlled_buffer_52
  assign BusB = BB20 ? R20 : 32'bz;  // Controlled_Buffer controlled_buffer_53
  assign BusB = BB21 ? R21 : 32'bz;  // Controlled_Buffer controlled_buffer_54
  assign BusB = BB22 ? R22 : 32'bz;  // Controlled_Buffer controlled_buffer_55
  assign BusB = BB23 ? R23 : 32'bz;  // Controlled_Buffer controlled_buffer_56
  assign BusB = BB24 ? R24 : 32'bz;  // Controlled_Buffer controlled_buffer_57
  assign BusB = BB25 ? R25 : 32'bz;  // Controlled_Buffer controlled_buffer_58
  assign BusB = BB26 ? R26 : 32'bz;  // Controlled_Buffer controlled_buffer_59
  assign BusB = BB27 ? R27 : 32'bz;  // Controlled_Buffer controlled_buffer_60
  assign BusB = BB28 ? R28 : 32'bz;  // Controlled_Buffer controlled_buffer_61
  assign BusB = BB29 ? R29 : 32'bz;  // Controlled_Buffer controlled_buffer_62
  assign BusB = BB30 ? R30 : 32'bz;  // Controlled_Buffer controlled_buffer_63
  assign BusB = BB31 ? R31 : 32'bz;  // Controlled_Buffer controlled_buffer_64

  // Other names for the same wires on the sheet: BA15 = BA14; BB15 = BB14; R15_t = R14_t
endmodule
