// Logisim project SCP.circ as structural Verilog
module SCP (
);

  wire B, button_1_out, clock_1_out, J;
  wire [4:0] ImmL;
  wire [10:0] ImmH;
  wire [15:0] Imm16;
  wire [19:0] BranshPC, counter_1_q, JumpPC, PC, pc_1_1_outpcplus1;
  wire [31:0] Rs1;

  Clock #(.highDuration(3200)) clock_1 (.out(clock_1_out));
  Jump jump_1 (.initial_pc(PC), .Imm16(Imm16), .Rs1(Rs1), .Pc_jump(JumpPC));
  Multiplexer #(.select(2), .width(20), .enable("false")) multiplexer_1 (
    .in0(pc_1_1_outpcplus1), .in1(BranshPC), .in2(JumpPC), .in3({20{1'b0}}), .out(PC), .sel({J, B}));
  Counter #(.width(20), .max('hfffff)) counter_1 (
    .load(1'b0), .D(PC), .count(1'b1), .Q(counter_1_q), .clk(clock_1_out), .clr(button_1_out));  // open: carry
  Button button_1 (.out(button_1_out));
  PC_1 pc_1_1 (.Initial_Pc(counter_1_q), .OutPcPlus1(pc_1_1_outpcplus1));
  Branch_pc branch_pc_1 (.initial_pc(PC), .ImmL(ImmL), .ImmU(ImmH), .Pc_Branch(BranshPC));
endmodule

module Data_Memory (
  input  [31:0] Address,
  input  [31:0] Data_In,
  input  Memory_Write,
  input  Memory_Read,
  input  Clock,
  output [31:0] Data_Out
);

  RAM #(.addrWidth(20), .dataWidth(32), .bus("separate")) ram_1 (
    .addr(Address[19:0]), .din(Data_In), .data(Data_Out), .str(Memory_Write), .sel(1'b1), .clk(Clock),
    .ld(Memory_Read));  // open: clr
endmodule

module Instruction_Memory (
  input  [19:0] PC,
  output [31:0] _32_bit_iinstruction
);

  ROM #(.addrWidth(20), .dataWidth(32)) rom_1 (.addr(PC), .data(_32_bit_iinstruction));  // open: sel

  // Notes on the sheet:
  //   INSTRUCTION MEMORY
  //   contents of rom_1 (hex, n*v repeats v):
  //   1100011
endmodule

module Register_File (
  input  [4:0] Rs1,
  input  [4:0] Rs2,
  input  [4:0] Rd,
  input  [31:0] BusW,
  input  RegWrite,
  input  Clock,
  output [31:0] R1,
  output [31:0] R2,
  output [31:0] R3,
  output [31:0] R4,
  output [31:0] R5,
  output [31:0] R6,
  output [31:0] R7,
  output [31:0] R8,
  output [31:0] R9,
  output [31:0] R10,
  output [31:0] R11,
  output [31:0] R12,
  output [31:0] R13,
  output [31:0] R14,
  output [31:0] R15,
  output [31:0] R16,
  output [31:0] R17,
  output [31:0] R18,
  output [31:0] R19,
  output [31:0] R20,
  output [31:0] R21,
  output [31:0] R22,
  output [31:0] R23,
  output [31:0] R24,
  output [31:0] R25,
  output [31:0] R26,
  output [31:0] R27,
  output [31:0] R28,
  output [31:0] R29,
  output [31:0] R30,
  output [31:0] R31,
  output [31:0] BusA,
  output [31:0] BusB
);

  wire and_1_out, and_2_out, and_3_out, and_4_out, and_5_out, and_6_out, and_7_out, and_8_out, and_9_out,
       and_10_out, and_11_out, and_12_out, and_13_out, and_14_out, and_15_out, and_16_out, and_17_out,
       and_18_out, and_19_out, and_20_out, and_21_out, and_22_out, and_23_out, and_24_out, and_25_out,
       and_26_out, and_27_out, and_28_out, and_29_out, and_30_out, and_31_out, BA0, BA1, BA2, BA3, BA4, BA5,
       BA6, BA7, BA8, BA9, BA10, BA11, BA12, BA13, BA14, BA16, BA17, BA18, BA19, BA20, BA21, BA22, BA23,
       BA24, BA25, BA26, BA27, BA28, BA29, BA30, BA31, BB0, BB1, BB2, BB3, BB4, BB5, BB6, BB7, BB8, BB9,
       BB10, BB11, BB12, BB13, BB14, BB16, BB17, BB18, BB19, BB20, BB21, BB22, BB23, BB24, BB25, BB26, BB27,
       BB28, BB29, BB30, BB31, R1_t, R2_t, R3_t, R4_t, R5_t, R6_t, R7_t, R8_t, R9_t, R10_t, R11_t, R12_t,
       R13_t, R14_t, R16_t, R17_t, R18_t, R19_t, R20_t, R21_t, R22_t, R23_t, R24_t, R25_t, R26_t, R27_t,
       R28_t, R29_t, R30_t, R31_t;

  Decoder #(.select(5), .tristate("true"), .disabled(0), .enable("false")) decoder_1 (
    .out1(R1_t), .out2(R2_t), .out3(R3_t), .out4(R4_t), .out5(R5_t), .out6(R6_t), .out7(R7_t), .out8(R8_t),
    .out9(R9_t), .out10(R10_t), .out11(R11_t), .out12(R12_t), .out13(R13_t), .out14(R14_t), .out15(R14_t),
    .out16(R16_t), .out17(R17_t), .out18(R18_t), .out19(R19_t), .out20(R20_t), .out21(R21_t), .out22(R22_t),
    .out23(R23_t), .out24(R24_t), .out25(R25_t), .out26(R26_t), .out27(R27_t), .out28(R28_t), .out29(R29_t),
    .out30(R30_t), .out31(R31_t), .sel(Rd));  // open: out0
  and and_1 (and_1_out, R1_t, RegWrite);
  and and_2 (and_2_out, R2_t, RegWrite);
  and and_3 (and_3_out, R3_t, RegWrite);
  and and_4 (and_4_out, R4_t, RegWrite);
  and and_5 (and_5_out, R5_t, RegWrite);
  and and_6 (and_6_out, R6_t, RegWrite);
  and and_7 (and_7_out, R7_t, RegWrite);
  and and_8 (and_8_out, R8_t, RegWrite);
  and and_9 (and_9_out, R9_t, RegWrite);
  and and_10 (and_10_out, R10_t, RegWrite);
  and and_11 (and_11_out, R11_t, RegWrite);
  and and_12 (and_12_out, R12_t, RegWrite);
  and and_13 (and_13_out, R13_t, RegWrite);
  and and_14 (and_14_out, R14_t, RegWrite);
  and and_15 (and_15_out, R14_t, RegWrite);
  and and_16 (and_16_out, R16_t, RegWrite);
  and and_17 (and_17_out, R17_t, RegWrite);
  and and_18 (and_18_out, R18_t, RegWrite);
  and and_19 (and_19_out, R19_t, RegWrite);
  and and_20 (and_20_out, R20_t, RegWrite);
  and and_21 (and_21_out, R21_t, RegWrite);
  and and_22 (and_22_out, R22_t, RegWrite);
  and and_23 (and_23_out, R23_t, RegWrite);
  and and_24 (and_24_out, R24_t, RegWrite);
  and and_25 (and_25_out, R25_t, RegWrite);
  and and_26 (and_26_out, R26_t, RegWrite);
  and and_27 (and_27_out, R27_t, RegWrite);
  and and_28 (and_28_out, R28_t, RegWrite);
  and and_29 (and_29_out, R29_t, RegWrite);
  and and_30 (and_30_out, R30_t, RegWrite);
  and and_31 (and_31_out, R31_t, RegWrite);
  Decoder #(.select(5), .tristate("true"), .disabled(0), .enable("false")) decoder_2 (
    .out0(BA0), .out1(BA1), .out2(BA2), .out3(BA3), .out4(BA4), .out5(BA5), .out6(BA6), .out7(BA7),
    .out8(BA8), .out9(BA9), .out10(BA10), .out11(BA11), .out12(BA12), .out13(BA13), .out14(BA14),
    .out15(BA14), .out16(BA16), .out17(BA17), .out18(BA18), .out19(BA19), .out20(BA20), .out21(BA21),
    .out22(BA22), .out23(BA23), .out24(BA24), .out25(BA25), .out26(BA26), .out27(BA27), .out28(BA28),
    .out29(BA29), .out30(BA30), .out31(BA31), .sel(Rs1));
  Register #(.width(32)) register_1 (.D(BusW), .en(and_1_out), .Q(R1), .clk(Clock));  // open: clr
  Register #(.width(32)) register_2 (.D(BusW), .en(and_2_out), .Q(R2), .clk(Clock));  // open: clr
  Register #(.width(32)) register_3 (.D(BusW), .en(and_3_out), .Q(R3), .clk(Clock));  // open: clr
  Register #(.width(32)) register_4 (.D(BusW), .en(and_4_out), .Q(R4), .clk(Clock));  // open: clr
  Register #(.width(32)) register_5 (.D(BusW), .en(and_5_out), .Q(R5), .clk(Clock));  // open: clr
  Register #(.width(32)) register_6 (.D(BusW), .en(and_6_out), .Q(R6), .clk(Clock));  // open: clr
  Register #(.width(32)) register_7 (.D(BusW), .en(and_7_out), .Q(R7), .clk(Clock));  // open: clr
  Register #(.width(32)) register_8 (.D(BusW), .en(and_8_out), .Q(R8), .clk(Clock));  // open: clr
  Register #(.width(32)) register_9 (.D(BusW), .en(and_9_out), .Q(R9), .clk(Clock));  // open: clr
  Register #(.width(32)) register_10 (.D(BusW), .en(and_10_out), .Q(R10), .clk(Clock));  // open: clr
  Register #(.width(32)) register_11 (.D(BusW), .en(and_11_out), .Q(R11), .clk(Clock));  // open: clr
  Register #(.width(32)) register_12 (.D(BusW), .en(and_12_out), .Q(R12), .clk(Clock));  // open: clr
  Register #(.width(32)) register_13 (.D(BusW), .en(and_13_out), .Q(R13), .clk(Clock));  // open: clr
  Register #(.width(32)) register_14 (.D(BusW), .en(and_14_out), .Q(R14), .clk(Clock));  // open: clr
  Register #(.width(32)) register_15 (.D(BusW), .en(and_15_out), .Q(R15), .clk(Clock));  // open: clr
  Register #(.width(32)) register_16 (.D(BusW), .en(and_16_out), .Q(R16), .clk(Clock));  // open: clr
  Register #(.width(32)) register_17 (.D(BusW), .en(and_17_out), .Q(R17), .clk(Clock));  // open: clr
  Register #(.width(32)) register_18 (.D(BusW), .en(and_18_out), .Q(R18), .clk(Clock));  // open: clr
  Register #(.width(32)) register_19 (.D(BusW), .en(and_19_out), .Q(R19), .clk(Clock));  // open: clr
  Register #(.width(32)) register_20 (.D(BusW), .en(and_20_out), .Q(R20), .clk(Clock));  // open: clr
  Register #(.width(32)) register_21 (.D(BusW), .en(and_21_out), .Q(R21), .clk(Clock));  // open: clr
  Register #(.width(32)) register_22 (.D(BusW), .en(and_22_out), .Q(R22), .clk(Clock));  // open: clr
  Register #(.width(32)) register_23 (.D(BusW), .en(and_23_out), .Q(R23), .clk(Clock));  // open: clr
  Register #(.width(32)) register_24 (.D(BusW), .en(and_24_out), .Q(R24), .clk(Clock));  // open: clr
  Register #(.width(32)) register_25 (.D(BusW), .en(and_25_out), .Q(R25), .clk(Clock));  // open: clr
  Register #(.width(32)) register_26 (.D(BusW), .en(and_26_out), .Q(R26), .clk(Clock));  // open: clr
  Register #(.width(32)) register_27 (.D(BusW), .en(and_27_out), .Q(R27), .clk(Clock));  // open: clr
  Register #(.width(32)) register_28 (.D(BusW), .en(and_28_out), .Q(R28), .clk(Clock));  // open: clr
  Register #(.width(32)) register_29 (.D(BusW), .en(and_29_out), .Q(R29), .clk(Clock));  // open: clr
  Register #(.width(32)) register_30 (.D(BusW), .en(and_30_out), .Q(R30), .clk(Clock));  // open: clr
  Register #(.width(32)) register_31 (.D(BusW), .en(and_31_out), .Q(R31), .clk(Clock));  // open: clr
  assign BusA = BA0 ? {32{1'b0}} : 32'bz;  // Controlled_Buffer controlled_buffer_1
  assign BusA = BA1 ? R1 : 32'bz;  // Controlled_Buffer controlled_buffer_2
  assign BusA = BA2 ? R2 : 32'bz;  // Controlled_Buffer controlled_buffer_3
  assign BusA = BA3 ? R3 : 32'bz;  // Controlled_Buffer controlled_buffer_4
  assign BusA = BA4 ? R4 : 32'bz;  // Controlled_Buffer controlled_buffer_5
  assign BusA = BA5 ? R5 : 32'bz;  // Controlled_Buffer controlled_buffer_6
  assign BusA = BA6 ? R6 : 32'bz;  // Controlled_Buffer controlled_buffer_7
  assign BusA = BA7 ? R7 : 32'bz;  // Controlled_Buffer controlled_buffer_8
  assign BusA = BA8 ? R8 : 32'bz;  // Controlled_Buffer controlled_buffer_9
  assign BusA = BA9 ? R9 : 32'bz;  // Controlled_Buffer controlled_buffer_10
  assign BusA = BA10 ? R10 : 32'bz;  // Controlled_Buffer controlled_buffer_11
  assign BusA = BA11 ? R11 : 32'bz;  // Controlled_Buffer controlled_buffer_12
  assign BusA = BA12 ? R12 : 32'bz;  // Controlled_Buffer controlled_buffer_13
  assign BusA = BA13 ? R13 : 32'bz;  // Controlled_Buffer controlled_buffer_14
  assign BusA = BA14 ? R14 : 32'bz;  // Controlled_Buffer controlled_buffer_15
  assign BusA = BA14 ? R15 : 32'bz;  // Controlled_Buffer controlled_buffer_16
  assign BusA = BA16 ? R16 : 32'bz;  // Controlled_Buffer controlled_buffer_17
  assign BusA = BA17 ? R17 : 32'bz;  // Controlled_Buffer controlled_buffer_18
  assign BusA = BA18 ? R18 : 32'bz;  // Controlled_Buffer controlled_buffer_19
  assign BusA = BA19 ? R19 : 32'bz;  // Controlled_Buffer controlled_buffer_20
  assign BusA = BA20 ? R20 : 32'bz;  // Controlled_Buffer controlled_buffer_21
  assign BusA = BA21 ? R21 : 32'bz;  // Controlled_Buffer controlled_buffer_22
  assign BusA = BA22 ? R22 : 32'bz;  // Controlled_Buffer controlled_buffer_23
  assign BusA = BA23 ? R23 : 32'bz;  // Controlled_Buffer controlled_buffer_24
  assign BusA = BA24 ? R24 : 32'bz;  // Controlled_Buffer controlled_buffer_25
  assign BusA = BA25 ? R25 : 32'bz;  // Controlled_Buffer controlled_buffer_26
  assign BusA = BA26 ? R26 : 32'bz;  // Controlled_Buffer controlled_buffer_27
  assign BusA = BA27 ? R27 : 32'bz;  // Controlled_Buffer controlled_buffer_28
  assign BusA = BA28 ? R28 : 32'bz;  // Controlled_Buffer controlled_buffer_29
  assign BusA = BA29 ? R29 : 32'bz;  // Controlled_Buffer controlled_buffer_30
  assign BusA = BA30 ? R30 : 32'bz;  // Controlled_Buffer controlled_buffer_31
  assign BusA = BA31 ? R31 : 32'bz;  // Controlled_Buffer controlled_buffer_32
  Decoder #(.select(5), .tristate("true"), .disabled(0), .enable("false")) decoder_3 (
    .out0(BB0), .out1(BB1), .out2(BB2), .out3(BB3), .out4(BB4), .out5(BB5), .out6(BB6), .out7(BB7),
    .out8(BB8), .out9(BB9), .out10(BB10), .out11(BB11), .out12(BB12), .out13(BB13), .out14(BB14),
    .out15(BB14), .out16(BB16), .out17(BB17), .out18(BB18), .out19(BB19), .out20(BB20), .out21(BB21),
    .out22(BB22), .out23(BB23), .out24(BB24), .out25(BB25), .out26(BB26), .out27(BB27), .out28(BB28),
    .out29(BB29), .out30(BB30), .out31(BB31), .sel(Rs2));
  assign BusB = BB0 ? {32{1'b0}} : 32'bz;  // Controlled_Buffer controlled_buffer_33
  assign BusB = BB1 ? R1 : 32'bz;  // Controlled_Buffer controlled_buffer_34
  assign BusB = BB2 ? R2 : 32'bz;  // Controlled_Buffer controlled_buffer_35
  assign BusB = BB3 ? R3 : 32'bz;  // Controlled_Buffer controlled_buffer_36
  assign BusB = BB4 ? R4 : 32'bz;  // Controlled_Buffer controlled_buffer_37
  assign BusB = BB5 ? R5 : 32'bz;  // Controlled_Buffer controlled_buffer_38
  assign BusB = BB6 ? R6 : 32'bz;  // Controlled_Buffer controlled_buffer_39
  assign BusB = BB7 ? R7 : 32'bz;  // Controlled_Buffer controlled_buffer_40
  assign BusB = BB8 ? R8 : 32'bz;  // Controlled_Buffer controlled_buffer_41
  assign BusB = BB9 ? R9 : 32'bz;  // Controlled_Buffer controlled_buffer_42
  assign BusB = BB10 ? R10 : 32'bz;  // Controlled_Buffer controlled_buffer_43
  assign BusB = BB11 ? R11 : 32'bz;  // Controlled_Buffer controlled_buffer_44
  assign BusB = BB12 ? R12 : 32'bz;  // Controlled_Buffer controlled_buffer_45
  assign BusB = BB13 ? R13 : 32'bz;  // Controlled_Buffer controlled_buffer_46
  assign BusB = BB14 ? R14 : 32'bz;  // Controlled_Buffer controlled_buffer_47
  assign BusB = BB14 ? R15 : 32'bz;  // Controlled_Buffer controlled_buffer_48
  assign BusB = BB16 ? R16 : 32'bz;  // Controlled_Buffer controlled_buffer_49
  assign BusB = BB17 ? R17 : 32'bz;  // Controlled_Buffer controlled_buffer_50
  assign BusB = BB18 ? R18 : 32'bz;  // Controlled_Buffer controlled_buffer_51
  assign BusB = BB19 ? R19 : 32'bz;  // Controlled_Buffer controlled_buffer_52
  assign BusB = BB20 ? R20 : 32'bz;  // Controlled_Buffer controlled_buffer_53
  assign BusB = BB21 ? R21 : 32'bz;  // Controlled_Buffer controlled_buffer_54
  assign BusB = BB22 ? R22 : 32'bz;  // Controlled_Buffer controlled_buffer_55
  assign BusB = BB23 ? R23 : 32'bz;  // Controlled_Buffer controlled_buffer_56
  assign BusB = BB24 ? R24 : 32'bz;  // Controlled_Buffer controlled_buffer_57
  assign BusB = BB25 ? R25 : 32'bz;  // Controlled_Buffer controlled_buffer_58
  assign BusB = BB26 ? R26 : 32'bz;  // Controlled_Buffer controlled_buffer_59
  assign BusB = BB27 ? R27 : 32'bz;  // Controlled_Buffer controlled_buffer_60
  assign BusB = BB28 ? R28 : 32'bz;  // Controlled_Buffer controlled_buffer_61
  assign BusB = BB29 ? R29 : 32'bz;  // Controlled_Buffer controlled_buffer_62
  assign BusB = BB30 ? R30 : 32'bz;  // Controlled_Buffer controlled_buffer_63
  assign BusB = BB31 ? R31 : 32'bz;  // Controlled_Buffer controlled_buffer_64

  // Other names for the same wires on the sheet: BA15 = BA14; BB15 = BB14; R15_t = R14_t
endmodule

module PC_1 (
  input  [19:0] Initial_Pc,
  output [19:0] OutPcPlus1
);

  Adder #(.width(20)) adder_1 (.a(Initial_Pc), .b(20'h1), .out(OutPcPlus1), .cin(1'b0));  // open: cout
endmodule

module Jump (
  input  [19:0] initial_pc,
  input  [15:0] Imm16,
  input  [31:0] Rs1,
  output [19:0] Pc_jump
);

  wire [19:0] bit_extender_1_out;

  assign bit_extender_1_out = {{4{1'b0}}, Imm16};  // Bit_Extender bit_extender_1
  Adder #(.width(20)) adder_1 (.a(bit_extender_1_out), .b(Rs1[19:0]), .out(Pc_jump), .cin(1'b0));  // open: cout

  // Notes on the sheet:
  //   JALR Rd,Rs1,imm16
endmodule

module Branch_pc (
  input  [4:0] ImmL,
  input  [10:0] ImmU,
  input  [19:0] initial_pc,
  output [19:0] Pc_Branch
);

  wire [19:0] bit_extender_1_out;

  assign bit_extender_1_out = {{4{1'b0}}, {ImmU, ImmL}};  // Bit_Extender bit_extender_1
  Adder #(.width(20)) adder_1 (.a(initial_pc), .b(bit_extender_1_out), .out(Pc_Branch), .cin(1'b0));  // open: cout
endmodule

module ALU (
  input  [31:0] Rs,
  input  [31:0] Rt,
  input  [19:0] ALU_Control,
  output Overflow,
  output [31:0] ALU_Output,
  output Zero,
  output Branch
);

  wire comparator_1_lt, comparator_2_lt, not_1_out, not_2_out, not_3_out;
  wire [31:0] arithmetic_unit_1_arith_output, Logic_unit_logic_output, SET_unit_logic_output,
       Shift_unit_shift_output;

  Comparator #(.width(32)) comparator_1 (.a(Rt), .b(Rs), .eq(Zero), .lt(comparator_1_lt));  // open: gt
  Comparator #(.width(32), .mode("unsigned")) comparator_2 (.a(Rt), .b(Rs), .lt(comparator_2_lt));  // open: gt, eq
  Arithmetic_unit arithmetic_unit_1 (
    .Rs(Rs), .Rt(Rt), .Arithmetic_Control(ALU_Control[5:0]), .Overflow(Overflow),
    .Arith_Output(arithmetic_unit_1_arith_output));  // open: Carryout
  Logic_unit Logic_unit (.Rs(Rs), .Rt(Rt), .Logic_Control(ALU_Control[9:6]), .Logic_Output(Logic_unit_logic_output));
  Shift_unit Shift_unit (.Rs(Rs), .Rt(Rt), .Shift_Control(ALU_Control[13:10]), .Shift_Output(Shift_unit_shift_output));
  SET_unit SET_unit (.Rt(Rt), .SET_Control(ALU_Control[17]), .Logic_Output(SET_unit_logic_output));  // open: Rs
  not not_1 (not_1_out, comparator_1_lt);
  not not_2 (not_2_out, comparator_2_lt);
  Multiplexer #(.select(2), .width(32)) multiplexer_1 (
    .in0(arithmetic_unit_1_arith_output), .in1(Logic_unit_logic_output), .in2(Shift_unit_shift_output),
    .in3(SET_unit_logic_output), .out(ALU_Output), .sel(ALU_Control[19:18]));  // open: en
  not not_3 (not_3_out, Zero);
  Multiplexer #(.select(3)) multiplexer_2 (
    .in0(1'b0), .in1(Zero), .in2(not_3_out), .in3(comparator_1_lt), .in4(not_1_out), .in5(comparator_2_lt),
    .in6(not_2_out), .out(Branch), .sel(ALU_Control[16:14]));  // open: in7, en

  // Notes on the sheet:
  //   BLT
  //   Arithmetic unit
  //   BEQ
  //   BGE
  //   BNE
  //   BLTU
  //   BGEU
endmodule

module Arithmetic_unit (
  input  [31:0] Rs,
  input  [31:0] Rt,
  input  [5:0] Arithmetic_Control,
  output Overflow,
  output Carryout,
  output [31:0] Arith_Output
);

  wire adder_1_cout, and_1_out, and_2_out, and_3_out, and_4_out, and_5_out, and_6_out, and_7_out, and_8_out,
       comparator_1_eq, comparator_1_lt, comparator_2_eq, comparator_3_gt, comparator_3_lt, comparator_4_gt,
       comparator_4_lt, comparator_5_gt, comparator_5_lt, comparator_6_gt, comparator_6_lt, comparator_7_gt,
       comparator_7_lt, or_5_out, or_6_out, subtractor_1_bout;
  wire [2:0] or_3_out;
  wire [31:0] ADD___ADDI, MUL, SEQ___SEQI, SLT___SLTI, SLTU___SLTIU, SUB;

  Adder #(.width(32)) adder_1 (.a(Rs), .b(Rt), .out(ADD___ADDI), .cout(adder_1_cout));  // open: cin
  Subtractor #(.width(32)) subtractor_1 (.a(Rs), .b(Rt), .out(SUB), .bout(subtractor_1_bout));  // open: bin
  Multiplier #(.width(32)) multiplier_1 (.a(Rs), .b(Rt), .out(MUL));  // open: cin, cout
  Comparator #(.width(32)) comparator_1 (.a(Rs), .b(Rt), .eq(comparator_1_eq), .lt(comparator_1_lt));  // open: gt
  Comparator #(.width(32), .mode("unsigned")) comparator_2 (.a(Rs), .b(Rt), .eq(comparator_2_eq));  // open: gt, lt
  assign SEQ___SEQI = {{31{1'b0}}, comparator_1_eq};  // Bit_Extender bit_extender_1
  assign SLT___SLTI = {{31{1'b0}}, comparator_1_lt};  // Bit_Extender bit_extender_2
  assign SLTU___SLTIU = {{31{1'b0}}, comparator_2_eq};  // Bit_Extender bit_extender_3
  // Probe on Arith_Output
  Multiplexer #(.select(3), .width(32)) multiplexer_1 (
    .in0(ADD___ADDI), .in1(SUB), .in2(SLT___SLTI), .in3(SLTU___SLTIU), .in4(SEQ___SEQI), .in5(MUL),
    .out(Arith_Output), .sel(or_3_out));  // open: in6, in7, en
  or or_1 (or_3_out[2], Arithmetic_Control[4], Arithmetic_Control[5]);
  or or_2 (or_3_out[1], Arithmetic_Control[2], Arithmetic_Control[3]);
  or or_3 (or_3_out[0], Arithmetic_Control[1], Arithmetic_Control[3], Arithmetic_Control[5]);
  Comparator #(.width(32)) comparator_3 (
    .a(Rs), .b({32{1'b0}}), .gt(comparator_3_gt), .lt(comparator_3_lt));  // open: eq
  Comparator #(.width(32)) comparator_4 (
    .a(Rt), .b({32{1'b0}}), .gt(comparator_4_gt), .lt(comparator_4_lt));  // open: eq
  Comparator #(.width(32)) comparator_5 (
    .a(ADD___ADDI), .b({32{1'b0}}), .gt(comparator_5_gt), .lt(comparator_5_lt));  // open: eq
  Comparator #(.width(32)) comparator_6 (
    .a(SUB), .b({32{1'b0}}), .gt(comparator_6_gt), .lt(comparator_6_lt));  // open: eq
  Comparator #(.width(32)) comparator_7 (.a(Rs), .b(Rt), .gt(comparator_7_gt), .lt(comparator_7_lt));  // open: eq
  and and_1 (and_1_out, comparator_3_gt, comparator_4_gt, comparator_5_lt);
  and and_2 (and_2_out, comparator_5_gt, comparator_4_lt, comparator_3_lt);
  and and_3 (and_3_out, comparator_6_lt, comparator_7_gt);
  and and_4 (and_4_out, comparator_6_gt, comparator_7_lt);
  and and_5 (and_5_out, adder_1_cout, Arithmetic_Control[0]);
  or or_4 (Carryout, and_5_out, and_6_out);
  and and_6 (and_6_out, subtractor_1_bout, Arithmetic_Control[0]);
  or or_5 (or_5_out, and_1_out, and_2_out);
  or or_6 (or_6_out, and_3_out, and_4_out);
  and and_7 (and_7_out, or_5_out, Arithmetic_Control[0]);
  or or_7 (Overflow, and_7_out, and_8_out);
  and and_8 (and_8_out, or_6_out, Arithmetic_Control[1]);
endmodule

module Logic_unit (
  input  [31:0] Rs,
  input  [31:0] Rt,
  input  [3:0] Logic_Control,
  output [31:0] Logic_Output
);

  wire [1:0] or_2_out;
  wire [31:0] AND___ANDI, NOR___NORI, OR___ORI, XOR___XORI;

  assign AND___ANDI = Rs & Rt;  // AND_Gate AND, 32 bits wide
  assign OR___ORI = Rs | Rt;  // OR_Gate OR, 32 bits wide
  assign NOR___NORI = ~(Rs | Rt);  // NOR_Gate NOR, 32 bits wide
  assign XOR___XORI = Rs ^ Rt;  // XOR_Gate XOR, 32 bits wide
  Multiplexer #(.select(2), .width(32)) multiplexer_1 (
    .in0(XOR___XORI), .in1(OR___ORI), .in2(AND___ANDI), .in3(NOR___NORI), .out(Logic_Output), .sel(or_2_out));  // open: en
  or or_2 (or_2_out[0], Logic_Control[1], Logic_Control[3]);
  or or_3 (or_2_out[1], Logic_Control[2], Logic_Control[3]);
endmodule

module Shift_unit (
  input  [31:0] Rs,
  input  [31:0] Rt,
  input  [3:0] Shift_Control,
  output [31:0] Shift_Output
);

  wire [1:0] or_1_out;
  wire [31:0] ROR____RORI, ROR___RORI, SLL___SLLI, SRA___SRAI, SRL___SRLI;

  Shifter #(.width(32)) shifter_1 (.in(Rs), .\dist (Rt[4:0]), .out(SLL___SLLI));
  Shifter #(.width(32), .shift("lr")) shifter_2 (.in(Rs), .\dist (Rt[4:0]), .out(SRL___SRLI));
  Shifter #(.width(32), .shift("ar")) shifter_3 (.in(Rs), .\dist (Rt[4:0]), .out(SRA___SRAI));
  Shifter #(.width(32), .shift("rr")) shifter_4 (.in(Rs), .\dist (Rt[4:0]), .out(ROR___RORI));
  Multiplexer #(.select(2), .width(32)) multiplexer_1 (
    .in0(SLL___SLLI), .in1(SRL___SRLI), .in2(SRA___SRAI), .in3(ROR____RORI), .out(Shift_Output),
    .sel(or_1_out));  // open: en
  or or_1 (or_1_out[0], Shift_Control[1], Shift_Control[3]);
  or or_2 (or_1_out[1], Shift_Control[2], Shift_Control[3]);

  // Notes on the sheet:
  //   SLL
endmodule

module SET_unit (
  input  [31:0] Rs,
  input  [31:0] Rt,
  input  SET_Control,
  output [31:0] Logic_Output
);

  wire [31:0] shifter_1_out, shifter_2_out, SSET;

  Shifter #(.width(32)) shifter_1 (.in(Rs), .\dist (5'b01111), .out(shifter_1_out));
  Multiplexer #(.width(32)) multiplexer_1 (.in0(Rt), .in1(SSET), .out(Logic_Output), .sel(SET_Control));  // open: en
  Shifter #(.width(32)) shifter_2 (.in(shifter_1_out), .\dist (5'b00001), .out(shifter_2_out));
  assign SSET = shifter_2_out | Rt;  // OR_Gate or_1, 32 bits wide

  // Other names for the same wires on the sheet: SET[31:0] = Rt
endmodule

module ALU_Control (
  input  [5:0] Opcode,
  input  [10:0] Function,
  output [19:0] ALU_Control
);

  wire and_1_out, and_2_out, and_3_out, and_4_out, and_5_out, and_6_out, and_9_out, and_10_out, and_11_out,
       and_12_out, and_14_out, and_15_out, and_16_out, and_17_out, and_18_out, and_19_out, and_21_out,
       and_22_out, and_23_out, and_24_out, and_25_out, and_26_out, and_27_out, and_28_out, and_29_out,
       and_30_out, and_31_out, and_32_out, and_33_out, and_34_out, and_35_out, nor_1_out, nor_2_out,
       nor_3_out, nor_4_out, nor_5_out, nor_6_out, nor_7_out, nor_8_out, nor_9_out, nor_10_out, nor_11_out,
       nor_12_out, nor_13_out, nor_14_out, nor_15_out, nor_16_out, nor_17_out, nor_18_out, nor_19_out,
       nor_20_out, nor_21_out, nor_22_out, nor_23_out, nor_24_out, nor_25_out, nor_26_out, nor_27_out,
       nor_28_out, nor_29_out, nor_30_out, nor_31_out, nor_32_out, nor_33_out, nor_34_out, not_1_out,
       not_2_out, or_16_out, or_17_out, or_18_out;

  not not_1 (not_1_out, Opcode[3]);
  nor nor_1 (nor_1_out, Opcode[0], Opcode[2], Opcode[3]);
  nor nor_2 (nor_2_out, Opcode[2], Opcode[3]);
  nor nor_3 (nor_3_out, Opcode[0], Opcode[1], Opcode[3]);
  nor nor_4 (nor_4_out, Opcode[1], Opcode[3]);
  nor nor_5 (nor_5_out, Opcode[0], Opcode[3]);
  and and_1 (and_1_out, not_1_out, Opcode[0], Opcode[1], Opcode[2], Opcode[4]);
  nor nor_6 (nor_6_out, Opcode[1], Opcode[4]);
  nor nor_7 (nor_7_out, Opcode[0], Opcode[4]);
  nor nor_8 (nor_8_out, Opcode[0], Opcode[1], Opcode[2], Opcode[3], Opcode[4], Function[0], Function[1], Function[3]);
  nor nor_9 (nor_9_out, Opcode[1], Opcode[3], Opcode[4]);
  not not_2 (not_2_out, Opcode[4]);
  nor nor_10 (nor_10_out, Opcode[1], Opcode[2], Opcode[3]);
  nor nor_11 (nor_11_out, Opcode[0], Opcode[1], Opcode[2], Opcode[3], Opcode[4], Function[1], Function[3]);
  nor nor_12 (nor_12_out, Opcode[0], Opcode[1], Opcode[2], Opcode[3], Opcode[4], Function[0], Function[3]);
  nor nor_13 (nor_13_out, Opcode[0], Opcode[3], Opcode[4]);
  nor nor_14 (nor_14_out, Opcode[0], Opcode[1], Opcode[2], Opcode[3], Opcode[4], Function[3]);
  nor nor_15 (nor_15_out, Opcode[3], Opcode[4]);
  nor nor_16 (nor_16_out, Opcode[0], Opcode[1], Opcode[2], Opcode[3], Opcode[4], Function[0], Function[1], Function[2]);
  nor nor_17 (nor_17_out, Opcode[0], Opcode[1], Opcode[2], Opcode[4]);
  nor nor_18 (nor_18_out, Opcode[0], Opcode[1], Opcode[2], Opcode[3], Opcode[4], Function[1]);
  nor nor_19 (nor_19_out, Opcode[1], Opcode[2], Opcode[3], Opcode[4]);
  nor nor_20 (nor_20_out, Opcode[0], Opcode[1], Opcode[2], Opcode[3], Opcode[4], Function[1], Function[2], Function[3]);
  nor nor_21 (nor_21_out, Opcode[0], Opcode[2], Opcode[3], Opcode[4]);
  nor nor_22 (nor_22_out, Opcode[0], Opcode[1], Opcode[2], Opcode[3], Opcode[4], Function[0], Function[2], Function[3]);
  nor nor_23 (nor_23_out, Opcode[2], Opcode[3], Opcode[4]);
  nor nor_24 (nor_24_out, Opcode[0], Opcode[1], Opcode[2], Opcode[3], Opcode[4], Function[2], Function[3]);
  nor nor_25 (nor_25_out, Opcode[0], Opcode[1], Opcode[3], Opcode[4]);
  nor nor_26 (nor_26_out, Opcode[0], Opcode[1], Opcode[2], Opcode[3], Opcode[4], Function[1], Function[2]);
  nor nor_27 (nor_27_out, Opcode[1], Opcode[2], Opcode[4]);
  nor nor_28 (nor_28_out, Opcode[0], Opcode[1], Opcode[2], Opcode[3], Opcode[4], Function[0], Function[2]);
  nor nor_29 (nor_29_out, Opcode[0], Opcode[2], Opcode[4]);
  nor nor_30 (nor_30_out, Opcode[0], Opcode[1], Opcode[2], Opcode[3], Opcode[4], Function[2]);
  nor nor_31 (nor_31_out, Opcode[2], Opcode[4]);
  nor nor_32 (nor_32_out, Opcode[0], Opcode[1], Opcode[2], Opcode[3], Opcode[4], Function[0], Function[1]);
  nor nor_33 (nor_33_out, Opcode[0], Opcode[1], Opcode[4]);
  and and_2 (and_2_out, nor_1_out, Opcode[1], Opcode[4]);
  and and_3 (and_3_out, nor_2_out, Opcode[0], Opcode[1], Opcode[4]);
  and and_4 (and_4_out, nor_3_out, Opcode[2], Opcode[4]);
  and and_5 (and_5_out, nor_4_out, Opcode[0], Opcode[2], Opcode[4]);
  and and_6 (and_6_out, nor_5_out, Opcode[1], Opcode[2], Opcode[4]);
  // AND_Gate and_7 has open pins: in0=nor_6_out, in1=Opcode[0], in2=Opcode[2], in3=Opcode[3], out=open
  and and_8 (ALU_Control[17], nor_7_out, Opcode[1], Opcode[2], Opcode[3]);
  and and_9 (and_9_out, nor_8_out, Function[2]);
  and and_10 (and_10_out, nor_9_out, Opcode[0], Opcode[2]);
  and and_11 (and_11_out, not_2_out, Opcode[0], Opcode[1], Opcode[2], Opcode[3]);
  and and_12 (and_12_out, nor_10_out, Opcode[0], Opcode[4]);
  and and_13 (ALU_Control[1], nor_11_out, Function[0], Function[2]);
  and and_14 (and_14_out, nor_12_out, Function[1], Function[2]);
  or or_1 (ALU_Control[2], and_14_out, and_15_out);
  and and_15 (and_15_out, nor_13_out, Opcode[1], Opcode[2]);
  and and_16 (and_16_out, nor_14_out, Function[0], Function[1], Function[2]);
  and and_17 (and_17_out, nor_15_out, Opcode[0], Opcode[1], Opcode[2]);
  and and_18 (and_18_out, nor_16_out, Function[3]);
  or or_2 (ALU_Control[4], and_18_out, and_19_out);
  and and_19 (and_19_out, nor_17_out, Opcode[3]);
  and and_20 (ALU_Control[5], nor_18_out, Function[0], Function[2], Function[3]);
  nor nor_34 (nor_34_out, Opcode[0], Opcode[1], Opcode[2], Opcode[3], Function[0], Function[1], Function[2], Function[3]);
  or or_3 (ALU_Control[6], nor_34_out, and_21_out);
  and and_21 (and_21_out, nor_19_out, Opcode[0]);
  and and_22 (and_22_out, nor_20_out, Function[0]);
  or or_4 (ALU_Control[7], and_22_out, and_23_out);
  and and_23 (and_23_out, nor_21_out, Opcode[1]);
  and and_24 (and_24_out, nor_22_out, Function[1]);
  or or_5 (ALU_Control[8], and_24_out, and_25_out);
  and and_25 (and_25_out, nor_23_out, Opcode[0], Opcode[1]);
  and and_26 (and_26_out, nor_24_out, Function[0], Function[1]);
  or or_6 (ALU_Control[9], and_26_out, and_27_out);
  and and_27 (and_27_out, nor_25_out, Opcode[2]);
  and and_28 (and_28_out, nor_26_out, Function[0], Function[3]);
  or or_7 (ALU_Control[10], and_28_out, and_29_out);
  and and_29 (and_29_out, nor_27_out, Opcode[0], Opcode[3]);
  and and_30 (and_30_out, nor_28_out, Function[1], Function[3]);
  or or_8 (ALU_Control[11], and_30_out, and_31_out);
  and and_31 (and_31_out, nor_29_out, Opcode[1], Opcode[3]);
  and and_32 (and_32_out, nor_30_out, Function[0], Function[1], Function[3]);
  and and_33 (and_33_out, nor_31_out, Opcode[0], Opcode[1], Opcode[3]);
  and and_34 (and_34_out, nor_32_out, Function[2], Function[3]);
  or or_9 (ALU_Control[13], and_34_out, and_35_out);
  and and_35 (and_35_out, nor_33_out, Opcode[2], Opcode[3]);
  or or_10 (ALU_Control[0], and_9_out, and_10_out, and_11_out, and_12_out);
  or or_11 (ALU_Control[3], and_16_out, and_17_out);
  or or_12 (ALU_Control[12], and_32_out, and_33_out);
  or or_13 (ALU_Control[14], and_2_out, and_4_out, and_6_out);
  or or_14 (ALU_Control[15], and_3_out, and_4_out, and_1_out);
  or or_15 (ALU_Control[16], and_5_out, and_6_out, and_1_out);
  or or_16 (or_16_out, ALU_Control[0], ALU_Control[1], ALU_Control[2], ALU_Control[3], ALU_Control[4], ALU_Control[5]);
  or or_17 (or_17_out, ALU_Control[6], ALU_Control[7], ALU_Control[8], ALU_Control[9]);
  or or_18 (or_18_out, ALU_Control[10], ALU_Control[11], ALU_Control[12], ALU_Control[13]);
  or or_19 (ALU_Control[18], or_16_out, or_18_out, ALU_Control[17]);
  or or_20 (ALU_Control[19], or_17_out, or_18_out, ALU_Control[17]);

  // Notes on the sheet:
  //   BEQ
  //   BNE
  //   BLT
  //   BGE
  //   BLTU
  //   BGEU
  //   SET
  //   SSET
  //   SUB
  //   MUL
  //   ADD_ADDI
  //   SLT_SLTI
  //   SLTU_SLTIU
  //   SEQ_SEQI
  //   SLL_SLLI
  //   SRL_SRLI
  //   SRA_SRAI
  //   ROR_RORI
  //   XOR_XORI
  //   OR_ORI
  //   AND_ANDI
  //   NOR_NORI
  //   Arithmetic Control
  //   Logic Control
  //   ALU MUX Control
  //   Shift Control
  //   Branch Control
  //   SET Control
endmodule

module Storage_Control_Unit (
  input  [5:0] in_1,
  output RegSrc,
  output RegWr,
  output MemRd,
  output MemWr,
  output MemtoReg
);

  wire and_1_out, and_2_out, and_3_out, and_4_out, not_1_out, not_2_out, not_3_out, not_4_out, not_5_out,
       not_6_out, not_7_out, not_8_out, not_9_out, not_10_out, not_11_out, not_12_out, not_13_out,
       not_14_out, not_15_out, not_16_out, not_17_out, not_18_out, not_19_out, not_20_out, not_21_out,
       not_22_out, not_23_out, not_24_out;

  not not_1 (not_1_out, in_1[5]);
  not not_2 (not_2_out, in_1[4]);
  not not_3 (not_3_out, in_1[0]);
  not not_4 (not_4_out, in_1[5]);
  not not_5 (not_5_out, in_1[3]);
  not not_6 (not_6_out, in_1[1]);
  not not_7 (not_7_out, in_1[5]);
  not not_8 (not_8_out, in_1[4]);
  not not_9 (not_9_out, in_1[5]);
  not not_10 (not_10_out, in_1[3]);
  not not_11 (not_11_out, in_1[2]);
  not not_12 (not_12_out, in_1[1]);
  not not_13 (not_13_out, in_1[0]);
  not not_14 (not_14_out, in_1[5]);
  not not_15 (not_15_out, in_1[3]);
  not not_16 (not_16_out, in_1[2]);
  not not_17 (not_17_out, in_1[1]);
  not not_18 (not_18_out, in_1[0]);
  not not_19 (not_19_out, in_1[5]);
  not not_20 (not_20_out, in_1[3]);
  not not_21 (not_21_out, in_1[2]);
  not not_22 (not_22_out, in_1[1]);
  not not_23 (not_23_out, in_1[5]);
  not not_24 (not_24_out, in_1[3]);
  and and_1 (and_1_out, not_1_out, not_2_out, in_1[3], in_1[2], in_1[1], not_3_out);
  and and_2 (and_2_out, not_4_out, in_1[4], not_5_out, in_1[2], not_6_out, in_1[0]);
  and and_3 (and_3_out, not_7_out, not_8_out);
  and and_4 (and_4_out, not_9_out, not_10_out, not_11_out, not_12_out, not_13_out);
  and and_5 (MemRd, not_14_out, in_1[4], not_15_out, not_16_out, not_17_out, not_18_out);
  and and_6 (MemWr, not_19_out, in_1[4], not_20_out, not_21_out, not_22_out, in_1[0]);
  and and_7 (MemtoReg, not_23_out, in_1[4], not_24_out);
  or or_1 (RegSrc, and_1_out, and_2_out);
  or or_2 (RegWr, and_3_out, and_4_out);

  // Other names for the same wires on the sheet: Op0 = in_1[0]; Op1 = in_1[1]; Op2 = in_1[2]; Op3 = in_1[3];
  //   Op4 = in_1[4]; Op5 = in_1[5]
endmodule

module Op_Control (
  input  [5:0] _6_bit_Op,
  output ExtOp,
  output ALUSrc
);

  wire and_1_out, and_2_out, and_3_out, and_4_out, and_5_out, and_6_out, and_7_out, and_8_out, and_9_out,
       and_10_out, not_1_out, not_2_out, not_3_out, not_4_out, not_5_out, not_6_out, not_7_out, not_8_out,
       not_9_out, not_10_out, not_11_out, not_12_out, not_13_out, not_14_out, not_15_out;

  not not_1 (not_1_out, _6_bit_Op[4]);
  not not_2 (not_2_out, _6_bit_Op[2]);
  not not_3 (not_3_out, _6_bit_Op[1]);
  not not_4 (not_4_out, _6_bit_Op[0]);
  not not_5 (not_5_out, _6_bit_Op[4]);
  not not_6 (not_6_out, _6_bit_Op[1]);
  not not_7 (not_7_out, _6_bit_Op[4]);
  not not_8 (not_8_out, _6_bit_Op[0]);
  not not_9 (not_9_out, _6_bit_Op[4]);
  not not_10 (not_10_out, _6_bit_Op[3]);
  not not_11 (not_11_out, _6_bit_Op[3]);
  not not_12 (not_12_out, _6_bit_Op[3]);
  not not_13 (not_13_out, _6_bit_Op[3]);
  not not_14 (not_14_out, _6_bit_Op[4]);
  not not_15 (not_15_out, _6_bit_Op[3]);
  and and_1 (and_1_out, not_1_out, not_2_out, not_3_out, not_4_out);
  and and_2 (and_2_out, not_5_out, _6_bit_Op[2], not_6_out, _6_bit_Op[0]);
  and and_3 (and_3_out, not_7_out, _6_bit_Op[2], _6_bit_Op[1], not_8_out);
  and and_4 (and_4_out, not_9_out, _6_bit_Op[3], _6_bit_Op[2], _6_bit_Op[1]);
  and and_5 (and_5_out, _6_bit_Op[4], not_10_out);
  and and_6 (and_6_out, not_11_out, _6_bit_Op[0]);
  and and_7 (and_7_out, not_12_out, _6_bit_Op[1]);
  and and_8 (and_8_out, not_13_out, _6_bit_Op[2]);
  and and_9 (and_9_out, not_14_out, _6_bit_Op[3]);
  and and_10 (and_10_out, _6_bit_Op[4], not_15_out);
  or or_1 (ExtOp, and_1_out, and_2_out, and_3_out, and_4_out, and_5_out);
  or or_2 (ALUSrc, and_6_out, and_7_out, and_8_out, and_9_out, and_10_out);

  // Other names for the same wires on the sheet: Op0 = _6_bit_Op[0]; Op1 = _6_bit_Op[1]; Op2 = _6_bit_Op[2];
  //   Op3 = _6_bit_Op[3]; Op4 = _6_bit_Op[4]
endmodule

module Extender (
  input  [15:0] Immediate,
  input  Extender_Op,
  output [31:0] Immediate_2
);

  wire [31:0] bit_extender_1_out, bit_extender_2_out;

  assign bit_extender_1_out = {{16{1'b0}}, Immediate};  // Bit_Extender bit_extender_1
  assign bit_extender_2_out = {{16{Immediate[15]}}, Immediate};  // Bit_Extender bit_extender_2
  Multiplexer #(.width(32)) multiplexer_1 (
    .in0(bit_extender_1_out), .in1(bit_extender_2_out), .out(Immediate_2), .sel(Extender_Op));  // open: en
endmodule

module PC_Control_unit (
  input  [5:0] in_1,
  output out_2,
  output out_3,
  output [1:0] out_4
);

  J_Branch j_branch_1 (._6_bit_Op(in_1), .Branch(out_2), .Jump(out_3));
  Pc_Src pc_src_1 (._6_bit_Op(in_1), .PC_Src0(out_4[0]), .Pc_Src1(out_4[1]));
endmodule

module Pc_Src (
  input  [5:0] _6_bit_Op,
  output PC_Src0,
  output Pc_Src1
);

  wire and_1_out, and_2_out, and_3_out, and_4_out, not_1_out, not_2_out, not_3_out, not_4_out, not_5_out,
       not_6_out, not_7_out, not_8_out, not_9_out, not_10_out, not_11_out;

  not not_1 (not_1_out, _6_bit_Op[4]);
  not not_2 (not_2_out, _6_bit_Op[2]);
  not not_3 (not_3_out, _6_bit_Op[4]);
  not not_4 (not_4_out, _6_bit_Op[1]);
  not not_5 (not_5_out, _6_bit_Op[4]);
  not not_6 (not_6_out, _6_bit_Op[0]);
  not not_7 (not_7_out, _6_bit_Op[3]);
  not not_8 (not_8_out, _6_bit_Op[2]);
  not not_9 (not_9_out, _6_bit_Op[1]);
  and and_1 (and_1_out, not_1_out, not_2_out);
  and and_2 (and_2_out, not_3_out, not_4_out);
  and and_3 (and_3_out, not_5_out, not_6_out);
  not not_10 (not_10_out, _6_bit_Op[3]);
  not not_11 (not_11_out, _6_bit_Op[4]);
  and and_4 (and_4_out, not_7_out, not_8_out, not_9_out);
  or or_1 (PC_Src0, and_1_out, and_2_out, and_3_out, not_10_out);
  or or_2 (Pc_Src1, not_11_out, and_4_out);

  // Other names for the same wires on the sheet: Op0 = _6_bit_Op[0]; Op1 = _6_bit_Op[1]; Op2 = _6_bit_Op[2];
  //   Op3 = _6_bit_Op[3]; Op4 = _6_bit_Op[4]
endmodule

module J_Branch (
  input  [5:0] _6_bit_Op,
  output Branch,
  output Jump
);

  wire and_1_out, and_2_out, not_1_out, not_2_out, not_3_out;

  not not_1 (not_1_out, _6_bit_Op[3]);
  not not_2 (not_2_out, _6_bit_Op[3]);
  not not_3 (not_3_out, _6_bit_Op[4]);
  and and_1 (and_1_out, _6_bit_Op[4], not_1_out, _6_bit_Op[1]);
  and and_2 (and_2_out, _6_bit_Op[4], not_2_out, _6_bit_Op[2]);
  and and_3 (Jump, not_3_out, _6_bit_Op[3], _6_bit_Op[2], _6_bit_Op[1], _6_bit_Op[0]);
  or or_1 (Branch, and_1_out, and_2_out);

  // Other names for the same wires on the sheet: Op0 = _6_bit_Op[0]; Op1 = _6_bit_Op[1]; Op2 = _6_bit_Op[2];
  //   Op3 = _6_bit_Op[3]; Op4 = _6_bit_Op[4]
endmodule

module Control_Signal_Unit (
  input  [5:0] OP6,
  output out_2,
  output out_3,
  output out_4,
  output out_5,
  output out_6,
  output out_7,
  output out_8,
  output out_9
);

  J_Branch j_branch_1 (._6_bit_Op(OP6), .Jump(out_2));  // open: Branch
  Storage_Control_Unit storage_control_unit_1 (
    .RegSrc(out_3), .RegWr(out_4), .MemRd(out_5), .MemWr(out_6), .MemtoReg(out_7), .in_1(OP6));
  Op_Control op_control_1 (._6_bit_Op(OP6), .ExtOp(out_8), .ALUSrc(out_9));
endmodule
