// Logisim project Single_Cycle_Processor.circ as structural Verilog: 3 circuits, main circuit Single_Cycle_Processor
module Single_Cycle_Processor (
);

  wire alu_1_p5, alu_control_1_p3, ALUSrc, B, button_1_out, clock_1_out, Ext, ImmSelect, J, MemRd, MemWr,
       register_file_1_p35, register_file_1_p39, RegSource, RegWr;
  wire [1:0] MemtoReg;
  wire [4:0] ImmL, instruction_spliter_1_rd, instruction_spliter_1_rs1, instruction_spliter_1_rs2,
       multiplexer_2_out;
  wire [5:0] OpCode;
  wire [10:0] Function, ImmH, ImmU;
  wire [15:0] Imm16;
  wire [19:0] BranshPC, JumpPC, multiplexer_1_out, PC, PC_1;
  wire [31:0] ALUOut, data_memory_1_data_out, Ext_PC, Extended, multiplexer_3_out, Output, R1, R2, R3, R4,
       R5, R6, R7, R8, R9, R10, R11, R12, R13, R14, R15, R16, R17, R18, R19, R20, R21, R22, R23, R24, R25,
       R26, R27, R28, R29, R30, R31, Rs1, Rs2, undriven;

  Multiplexer #(.select(2), .width(20), .enable("false")) multiplexer_1 (
    .in0(PC_1), .in1(BranshPC), .in2(JumpPC), .in3({20{1'b0}}), .out(multiplexer_1_out), .sel({J, B}));
  Jump jump_1 (.Imm16(Imm16), .Pc_jump(JumpPC), .Rs1(Rs1));
  Register #(.width(20)) Register (.D(multiplexer_1_out), .en(1'b1), .Q(PC), .clk(clock_1_out), .clr(button_1_out));
  Button button_1 (.out(button_1_out));
  PC_1 pc_1_1 (.Initial_Pc(PC), .OutPcPlus1(PC_1));
  Control_Signal_Unit control_signal_unit_1 (
    .OP6(OpCode), .out_2(J), .out_4(RegWr), .out_5(MemRd), .out_6(MemWr), .out_7(MemtoReg), .out_8(Ext),
    .out_9(ALUSrc), .out_10(ImmSelect), .out_3(RegSource));
  // Probe on PC
  Branch_pc branch_pc_1 (.ImmL(ImmL), .ImmU(ImmH), .initial_pc(PC), .Pc_Branch(BranshPC));
  // Instruction_Memory instruction_memory_1: pin names not known; wires that end beside it: PC
  // Probe on Function
  // Probe on Imm16
  // Probe on R1
  // Probe on R2
  // Probe on R3
  // Probe on R4
  // Probe on R5
  // Probe on R6
  // Probe on R7
  // Probe on R8
  Instruction_Spliter instruction_spliter_1 (
    .in_1(undriven), .Opcode(OpCode), .RD(instruction_spliter_1_rd), .ImmL(ImmL),
    .Rs1(instruction_spliter_1_rs1), .Rs2(instruction_spliter_1_rs2), .ImmU(ImmU), .F(Function), .Imm16(Imm16));
  // Probe on OpCode
  // Probe on ImmU
  // Probe on multiplexer_2_out
  Multiplexer #(.width(5), .enable("false")) multiplexer_2 (
    .in0(instruction_spliter_1_rs1), .in1(instruction_spliter_1_rd), .out(multiplexer_2_out), .sel(RegSource));
  // Probe on instruction_spliter_1_rs2
  // Probe on instruction_spliter_1_rd
  // Probe on ImmL
  // Probe on R9
  // Probe on R10
  // Probe on R11
  // Probe on R12
  // Probe on R13
  // Probe on R14
  // Probe on R15
  // Probe on R16
  Clock clock_1 (.out(clock_1_out));
  // Probe on R17
  // Probe on R18
  // Probe on R19
  // Probe on R20
  // Probe on R21
  // Probe on R22
  // Probe on R23
  // Probe on R24
  // Register_File register_file_1: pin names not known; wires that end beside it: multiplexer_2_out, instruction_spliter_1_rs2, instruction_spliter_1_rd, R1, R2, R3, R4, R5, clock_1_out, R6, R7, R8, R9, R10, R11, R12, R13, R14, R15, R16, R17, RegWr, R18, R19, R20, R21, R22, R23, R24, R25, R26, R27, Output, R28, register_file_1_p35, R29, R30, R31, register_file_1_p39, register_file_1_p35, Rs2
  // Probe on R25
  // Probe on R26
  // Probe on R27
  // Probe on R28
  // Probe on R29
  // Probe on R30
  // Probe on R31
  // Probe on Rs2
  // Probe on register_file_1_p39
  // Probe on multiplexer_3_out
  Multiplexer #(.width(32), .enable("false")) multiplexer_3 (
    .in0(Rs2), .in1(Extended), .out(multiplexer_3_out), .sel(ALUSrc));
  // ALU_Control alu_control_1: pin names not known; wires that end beside it: OpCode, Function, alu_control_1_p3
  // ALU alu_1: pin names not known; wires that end beside it: register_file_1_p39, multiplexer_3_out, B, alu_control_1_p3, alu_1_p5, alu_1_p5, ALUOut
  // Probe on ALUOut
  Extender extender_1 (
    .Extender_Op(Ext), .Immediate(Extended), .Imm16(Imm16), .ImmSelect(ImmSelect), .ImmU(ImmU), .ImmL(ImmL),
    .PC_1(PC_1), .PC_Extended(Ext_PC));
  Data_Memory data_memory_1 (
    .Address(ALUOut), .Data_In(Rs2), .Memory_Write(MemWr), .Clock(clock_1_out),
    .Data_Out(data_memory_1_data_out), .Memory_Read(MemRd));
  Multiplexer #(.select(2), .width(32), .enable("false")) multiplexer_4 (
    .in0(ALUOut), .in1(data_memory_1_data_out), .in2(Ext_PC), .out(Output), .sel(MemtoReg));  // open: in3
  // Probe on Output
endmodule

module Instruction_Spliter (
  input  [31:0] in_1,
  output [5:0] Opcode,
  output [4:0] RD,
  output [4:0] ImmL,
  output [4:0] Rs1,
  output [15:0] Imm16,
  output [10:0] F,
  output [10:0] ImmU,
  output [4:0] Rs2
);


  assign F = in_1[31:21];
  assign Imm16 = in_1[31:16];
  assign ImmL = in_1[10:6];
  assign ImmU = in_1[31:21];
  assign Opcode = in_1[5:0];
  assign RD = in_1[10:6];
  assign Rs1 = in_1[15:11];
  assign Rs2 = in_1[20:16];

  // Notes on the sheet:
  //   SB_Type
  //   R_Tube
  //   I-Type
endmodule

module temp (
  input  [31:0] in_1,
  input  [31:0] in_2,
  input  [5:0] in_3,
  input  [10:0] in_4,
  output out_5,
  output out_6,
  output out_7,
  output [31:0] out_8
);

  wire ALUSrc, Ext, J, MemRd, MemtoReg, MemWr, RegSource, RegWr;
  wire [5:0] OpCode;
  wire [19:0] alu_control_1_alu_control;

  ALU_Control alu_control_1 (.Opcode(in_3), .Function(in_4), .ALU_Control(alu_control_1_alu_control));
  ALU alu_1 (
    .Rs(in_1), .Rt(in_2), .Overflow(out_5), .ALU_Output(out_8), .Branch(out_7), .Zero(out_6),
    .ALU_Control(alu_control_1_alu_control));
  Storage_Control_Unit storage_control_unit_1 (
    .RegSrc(RegSource), .RegWr(RegWr), .MemRd(MemRd), .MemWr(MemWr), .MemtoReg(MemtoReg), .in_1(OpCode));
  Op_Control op_control_1 (.ExtOp(Ext), .ALUSrc(ALUSrc), ._6_bit_Op(OpCode));
  Pc_Control_Unit pc_control_unit_1 (.in_1(OpCode), .out_3(J));  // open: out_2, out_4
endmodule
