// Logisim project Storage Control.circ as structural Verilog: 1 circuit, main circuit Storage Control Unit
// Storage Control
module Storage_Control_Unit (
  input  [5:0] in_1,
  output RegSrc,
  output RegWr,
  output MemRd,
  output MemWr,
  output [1:0] MemtoReg
);

  wire and_1_out, and_2_out, and_3_out, and_4_out, not_1_out, not_2_out, not_3_out, not_4_out, not_5_out,
       not_6_out, not_7_out, not_8_out, not_9_out, not_10_out, not_11_out, not_12_out, not_13_out,
       not_14_out, not_15_out, not_16_out, not_17_out, not_18_out, not_19_out, not_20_out, not_21_out,
       not_22_out, not_23_out, not_24_out, not_25_out, not_26_out;

  not not_1 (not_1_out, in_1[5]);
  not not_2 (not_2_out, in_1[4]);
  not not_3 (not_3_out, in_1[0]);
  not not_4 (not_4_out, in_1[5]);
  not not_5 (not_5_out, in_1[3]);
  not not_6 (not_6_out, in_1[1]);
  not not_7 (not_7_out, in_1[5]);
  not not_8 (not_8_out, in_1[4]);
  not not_9 (not_9_out, in_1[5]);
  not not_10 (not_10_out, in_1[3]);
  not not_11 (not_11_out, in_1[2]);
  not not_12 (not_12_out, in_1[1]);
  not not_13 (not_13_out, in_1[0]);
  not not_14 (not_14_out, in_1[5]);
  not not_15 (not_15_out, in_1[3]);
  not not_16 (not_16_out, in_1[2]);
  not not_17 (not_17_out, in_1[1]);
  not not_18 (not_18_out, in_1[0]);
  not not_19 (not_19_out, in_1[5]);
  not not_20 (not_20_out, in_1[3]);
  not not_21 (not_21_out, in_1[2]);
  not not_22 (not_22_out, in_1[1]);
  not not_23 (not_23_out, in_1[5]);
  not not_24 (not_24_out, in_1[3]);
  not not_25 (not_25_out, in_1[4]);
  not not_26 (not_26_out, in_1[5]);
  and and_1 (and_1_out, not_1_out, not_2_out, in_1[3], in_1[2], in_1[1], not_3_out);
  and and_2 (and_2_out, not_4_out, in_1[4], not_5_out, in_1[2], not_6_out, in_1[0]);
  and and_3 (and_3_out, not_7_out, not_8_out);
  and and_4 (and_4_out, not_9_out, not_10_out, not_11_out, not_12_out, not_13_out);
  and and_5 (MemRd, not_14_out, in_1[4], not_15_out, not_16_out, not_17_out, not_18_out);
  and and_6 (MemWr, not_19_out, in_1[4], not_20_out, not_21_out, not_22_out, in_1[0]);
  and and_7 (MemtoReg[0], not_23_out, in_1[4], not_24_out);
  and and_8 (MemtoReg[1], in_1[0], in_1[1], in_1[2], in_1[3], not_25_out, not_26_out);
  or or_1 (RegSrc, and_1_out, and_2_out);
  or or_2 (RegWr, and_3_out, and_4_out);

  // Other names for the same wires on the sheet: Op0 = in_1[0]; Op1 = in_1[1]; Op2 = in_1[2]; Op3 = in_1[3];
  //   Op4 = in_1[4]; Op5 = in_1[5]
endmodule
