// Logisim project Third_try.circ as structural Verilog: 1 circuit, main circuit main
module main (
  input  [4:0] in_1,
  input  [10:0] in_2,
  input  [15:0] in_3,
  input  in_4,
  input  [31:0] Rs1,
  input  in_6,
  input  clk,
  output [19:0] OutPc,
  output [19:0] OutPcPlus1
);

  wire undriven;
  wire [19:0] bit_extender_1_out, bit_extender_2_out, initial_pc, multiplexer_1_out, OutPcPlus1_t, PC_branch,
       Pc_JALR;

  assign bit_extender_1_out = {{4{in_2[10]}}, {in_2, in_1}};  // Bit_Extender bit_extender_1
  assign bit_extender_2_out = {{4{in_3[15]}}, in_3};  // Bit_Extender bit_extender_2
  Register #(.width(20)) register_1 (.D(initial_pc), .en(1'b1), .clk(clk), .Q(OutPc));  // open: clr
  Adder #(.width(20)) adder_1 (.a(initial_pc), .b(bit_extender_1_out), .out(PC_branch), .cin(1'b0));  // open: cout
  Adder #(.width(20)) adder_2 (.a(bit_extender_2_out), .b(Rs1[19:0]), .out(Pc_JALR), .cin(1'b0));  // open: cout
  Adder #(.width(20)) adder_3 (.a(OutPc), .b(20'h1), .out(OutPcPlus1), .cin(1'b0));  // open: cout
  Multiplexer #(.width(20), .enable("false")) multiplexer_1 (
    .in0(OutPcPlus1_t), .in1(PC_branch), .out(multiplexer_1_out), .sel(undriven));
  Multiplexer #(.width(20), .enable("false")) multiplexer_2 (
    .in0(multiplexer_1_out), .in1(Pc_JALR), .out(initial_pc), .sel(in_4));

  // Notes on the sheet:
  //   JALR Rd,Rs1,imm16
  //   Pc
  //   PC_branch
  //   Next Pc
endmodule
